// Logisim project 4bit_swap.circ as structural Verilog: 2 circuits, main circuit main
module main (
  output [3:0] A,
  output [3:0] B,
  output [3:0] C,
  output [3:0] D,
  output [3:0] _1,
  output [3:0] _2,
  output [3:0] _3,
  output [3:0] _4,
  output Halt
);

  wire clock_1_out;
  wire [3:0] counter_1_q;

  Counter #(.width(4), .max('hf)) counter_1 (
    .Q(counter_1_q), .carry(Halt), .clk(clock_1_out));  // open: load, D, count, clr
  Clock clock_1 (.out(clock_1_out));
  ROM #(.addrWidth(4), .dataWidth(16)) rom_1 (.addr(counter_1_q), .data({_4, _3, _2, _1}));  // open: sel

  assign A = _1;
  assign B = _2;
  assign C = _3;
  assign D = _4;
endmodule

module swap (
  input  I_1,
  input  I_2,
  input  s,
  output out_4,
  output out_5
);

  wire and_1_out, and_2_out, and_3_out, and_4_out, buffer_1_out, buffer_2_out, not_1_out, not_2_out,
       not_3_out, not_4_out, not_5_out, not_6_out, xor_1_out, xor_2_out, xor_3_out, xor_4_out;

  not not_1 (not_1_out, s);
  not not_2 (not_2_out, s);
  xor xor_1 (xor_1_out, I_1, not_1_out);
  xor xor_2 (xor_2_out, I_2, not_2_out);
  not not_3 (not_3_out, s);
  not not_4 (not_4_out, s);
  xor xor_3 (xor_3_out, xor_1_out, not_3_out);
  not not_5 (not_5_out, s);
  xor xor_4 (xor_4_out, xor_2_out, not_4_out);
  not not_6 (not_6_out, s);
  buf buffer_1 (buffer_1_out, not_5_out);
  buf buffer_2 (buffer_2_out, not_6_out);
  and and_1 (and_1_out, xor_3_out, buffer_1_out);
  and and_2 (and_2_out, I_1, s);
  and and_3 (and_3_out, xor_4_out, buffer_2_out);
  and and_4 (and_4_out, I_2, s);
  or or_1 (out_4, and_1_out, and_4_out);
  or or_2 (out_5, and_3_out, and_2_out);
endmodule
