// Logisim project ALU_76066001.circ as structural Verilog: 2 circuits, main circuit main
module main (
  output [3:0] out_1,
  output out_2
);

  wire clock_1_out, clock_2_out;
  wire [1:0] counter_2_q;
  wire [7:0] counter_1_q, rom_1_data;

  Counter counter_1 (.Q(counter_1_q), .carry(out_2), .clk(clock_1_out));  // open: load, D, count, clr
  Clock clock_1 (.out(clock_1_out));
  ROM rom_1 (.addr(counter_1_q), .data(rom_1_data));  // open: sel
  Counter #(.width(2), .max('h3)) counter_2 (.Q(counter_2_q), .clk(clock_2_out));  // open: load, D, count, carry, clr
  Clock clock_2 (.out(clock_2_out));
  alu alu_1 (.in_1(rom_1_data[7:4]), .in_2(rom_1_data[3:0]), .in_3(counter_2_q), .out_4(out_1));
endmodule

module alu (
  input  [3:0] in_1,
  input  [3:0] in_2,
  input  [1:0] in_3,
  output [3:0] out_4
);

  wire [3:0] adder_1_out, and_1_out, or_1_out, subtractor_1_out;

  Adder #(.width(4)) adder_1 (.a(in_1), .b(in_2), .out(adder_1_out));  // open: cin, cout
  Subtractor #(.width(4)) subtractor_1 (.a(in_1), .b(in_2), .out(subtractor_1_out));  // open: bin, bout
  assign and_1_out = in_1 & in_2;  // AND_Gate and_1, 4 bits wide
  assign or_1_out = in_1 | in_2;  // OR_Gate or_1, 4 bits wide
  Multiplexer #(.select(2), .width(4)) multiplexer_1 (
    .in0(adder_1_out), .in1(subtractor_1_out), .in2(and_1_out), .in3(or_1_out), .out(out_4), .sel(in_3));  // open: en
endmodule
