// Logisim project CRC_76066001.circ as structural Verilog: 2 circuits, main circuit main
module main (
  output [7:0] out_1,
  output [3:0] out_2,
  output [10:0] out_3,
  output out_4
);

  wire clock_1_out;
  wire [3:0] counter_1_q;

  Clock clock_1 (.out(clock_1_out));
  Counter #(.width(4), .max('hf)) counter_1 (
    .Q(counter_1_q), .carry(out_4), .clk(clock_1_out));  // open: load, D, count, clr
  ROM #(.addrWidth(4), .dataWidth(12)) rom_1 (.addr(counter_1_q), .data({out_2, out_1}));  // open: sel
  CRC crc_1 (.in_1(out_1), .in_2(out_2), .out_3(out_3));
endmodule

module CRC (
  input  [7:0] in_1,
  input  [3:0] in_2,
  output [10:0] out_3
);

  wire [3:0] and_1_out, and_5_out, and_9_out, and_13_out, and_17_out, and_21_out, and_25_out, and_29_out,
       xor_1_out, xor_2_out, xor_3_out, xor_4_out, xor_5_out, xor_6_out, xor_7_out;
  wire [3:3] xor_8_out;

  and and_1 (and_1_out[0], in_1[7], in_2[0]);
  and and_2 (and_1_out[1], in_1[7], in_2[1]);
  and and_3 (and_1_out[2], in_1[7], in_2[2]);
  and and_4 (and_1_out[3], in_1[7], in_2[3]);
  assign xor_1_out = in_1[7:4] ^ and_1_out;  // XOR_Gate xor_1, 4 bits wide
  and and_5 (and_5_out[0], xor_1_out[2], in_2[0]);
  and and_6 (and_5_out[1], xor_1_out[2], in_2[1]);
  and and_7 (and_5_out[2], xor_1_out[2], in_2[2]);
  and and_8 (and_5_out[3], xor_1_out[2], in_2[3]);
  assign xor_2_out = {xor_1_out[2:0], in_1[3]} ^ and_5_out;  // XOR_Gate xor_2, 4 bits wide
  and and_9 (and_9_out[0], xor_2_out[2], in_2[0]);
  and and_10 (and_9_out[1], xor_2_out[2], in_2[1]);
  and and_11 (and_9_out[2], xor_2_out[2], in_2[2]);
  and and_12 (and_9_out[3], xor_2_out[2], in_2[3]);
  assign xor_3_out = {xor_2_out[2:0], in_1[2]} ^ and_9_out;  // XOR_Gate xor_3, 4 bits wide
  and and_13 (and_13_out[0], xor_3_out[2], in_2[0]);
  and and_14 (and_13_out[1], xor_3_out[2], xor_3_out[2], in_2[1]);
  and and_15 (and_13_out[2], xor_3_out[2], in_2[2]);
  and and_16 (and_13_out[3], xor_3_out[2], in_2[3]);
  assign xor_4_out = {xor_3_out[2:0], in_1[1]} ^ and_13_out;  // XOR_Gate xor_4, 4 bits wide
  and and_17 (and_17_out[0], xor_4_out[2], in_2[0]);
  and and_18 (and_17_out[1], xor_4_out[2], in_2[1]);
  and and_19 (and_17_out[2], xor_4_out[2], in_2[2]);
  and and_20 (and_17_out[3], xor_4_out[2], in_2[3]);
  assign xor_5_out = {xor_4_out[2:0], in_1[0]} ^ and_17_out;  // XOR_Gate xor_5, 4 bits wide
  and and_21 (and_21_out[0], xor_5_out[2], in_2[0]);
  and and_22 (and_21_out[1], xor_5_out[2], in_2[1]);
  and and_23 (and_21_out[2], xor_5_out[2], in_2[2]);
  and and_24 (and_21_out[3], xor_5_out[2], in_2[3]);
  assign xor_6_out = {xor_5_out[2:0], 1'b0} ^ and_21_out;  // XOR_Gate xor_6, 4 bits wide
  and and_25 (and_25_out[0], xor_6_out[2], in_2[0]);
  and and_26 (and_25_out[1], xor_6_out[2], in_2[1]);
  and and_27 (and_25_out[2], xor_6_out[2], xor_6_out[2], in_2[2]);
  and and_28 (and_25_out[3], xor_6_out[2], in_2[3]);
  assign xor_7_out = {xor_6_out[2:0], 1'b0} ^ and_25_out;  // XOR_Gate xor_7, 4 bits wide
  and and_29 (and_29_out[0], xor_7_out[2], in_2[0]);
  and and_30 (and_29_out[1], xor_7_out[2], in_2[1]);
  and and_31 (and_29_out[2], xor_7_out[2], xor_7_out[2], in_2[2]);
  and and_32 (and_29_out[3], xor_7_out[2], in_2[3]);
  assign {xor_8_out[3], out_3[2:0]} = {xor_7_out[2:0], 1'b0} ^ and_29_out;  // XOR_Gate xor_8, 4 bits wide

  assign out_3[10:3] = in_1;
endmodule
