// Logisim project FSM_76066001.circ as structural Verilog: 5 circuits, main circuit main
module main (
  input  [1:0] in_1,
  output out_2,
  output out_3,
  output out_4
);

  wire clock_1_out;
  wire [7:0] counter_1_q;

  Clock clock_1 (.out(clock_1_out));
  Counter counter_1 (.Q(counter_1_q), .carry(out_4), .clk(clock_1_out));  // open: load, D, count, clr
  ROM #(.dataWidth(3)) rom_1 (.addr(counter_1_q), .data({in_1, out_2}));  // open: sel
  fsm fsm_1 (.in_1(out_2), .in_2(in_1), .out_3(out_3));
endmodule

module fsm (
  input  in_1,
  input  [1:0] in_2,
  output out_3
);

  wire clock_1_out, clr_1_so1, clr_1_so2, d_ff_1_q, d_ff_2_q, mealy_1_so1, mealy_1_so2;

  Clock clock_1 (.out(clock_1_out));
  Mealy mealy_1 (
    .S1(d_ff_1_q), .S2(d_ff_2_q), .In1(in_2[1]), .In2(in_2[0]), .SO1(mealy_1_so1), .SO2(mealy_1_so2),
    .Output(out_3));
  clr clr_1 (.clr(in_1), .S1(mealy_1_so1), .S2(mealy_1_so2), .SO1(clr_1_so1), .SO2(clr_1_so2));
  D_Flip_Flop d_ff_1 (.clk(clock_1_out), .D(clr_1_so1), .Q(d_ff_1_q));  // open: Qn, preset, en, reset
  D_Flip_Flop d_ff_2 (.clk(clock_1_out), .D(clr_1_so2), .Q(d_ff_2_q));  // open: Qn, preset, en, reset
endmodule

module \output  (
  input  S1,
  input  S2,
  output Output_1
);

  and and_1 (Output_1, S1, S2);
endmodule

module clr (
  input  clr,
  input  S1,
  input  S2,
  output SO1,
  output SO2
);

  wire not_1_out, not_2_out;

  not not_1 (not_1_out, clr);
  not not_2 (not_2_out, clr);
  and and_1 (SO1, not_1_out, S1);
  and and_2 (SO2, not_2_out, S2);
endmodule

module Mealy (
  input  S1,
  input  S2,
  input  In1,
  input  In2,
  output SO1,
  output SO2,
  output Output
);

  wire and_1_out, and_2_out, and_3_out, and_4_out, not_1_out, not_2_out, not_3_out, not_4_out, not_5_out,
       not_6_out, not_7_out, not_8_out, not_9_out;

  not not_1 (not_1_out, S1);
  and and_1 (and_1_out, not_1_out, S2, not_2_out);
  not not_2 (not_2_out, In2);
  not not_3 (not_3_out, S2);
  and and_2 (and_2_out, S1, not_3_out, not_4_out);
  not not_4 (not_4_out, In2);
  not not_5 (not_5_out, In1);
  and and_3 (and_3_out, not_5_out, In2);
  not not_6 (not_6_out, S2);
  and and_4 (and_4_out, S1, not_6_out, not_7_out);
  not not_7 (not_7_out, In2);
  and and_5 (Output, S1, not_8_out, not_9_out);
  not not_8 (not_8_out, S2);
  not not_9 (not_9_out, In2);
  or or_1 (SO1, and_1_out, and_2_out);
  or or_2 (SO2, and_3_out, and_4_out);
endmodule
