// Logisim project Logisim circuit 1.circ as structural Verilog: 1 circuit, main circuit main
module main (
  input  A,
  input  B,
  input  Cin,
  output S,
  output Cout
);

  wire or_1_out, xor_1_out, xor_2_out;

  or or_1 (or_1_out, A, B);
  or or_2 (S, or_1_out, Cin);
  xor xor_1 (xor_1_out, Cin, or_1_out);
  and and_1 (Cout, xor_1_out, xor_2_out);
  xor xor_2 (xor_2_out, A, B);
endmodule
