// Logisim project Logisim circuit 2.circ as structural Verilog: 1 circuit, main circuit main
module main (
  input  in_1,
  input  [7:0] in_2,
  input  in_3,
  output out_4
);

  wire and_1_out, nor_1_out;

  nor nor_1 (nor_1_out, in_1, in_2[7]);
  and and_1 (and_1_out, in_2[0], in_3);
  and and_2 (out_4, nor_1_out, and_1_out);
endmodule
