// Logisim project Logisim circuit 3.circ as structural Verilog: 2 circuits, main circuit main
module main (
  output out_1
);

  wire clock_1_out;
  wire [2:0] counter_1_q, rom_1_data;

  Counter #(.width(3), .max('h7)) counter_1 (
    .Q(counter_1_q), .carry(out_1), .clk(clock_1_out));  // open: load, D, count, clr
  Clock clock_1 (.out(clock_1_out));
  ROM #(.addrWidth(3), .dataWidth(3)) rom_1 (.addr(counter_1_q), .data(rom_1_data));  // open: sel

  // Notes on the sheet:
  //   contents of rom_1 (hex, n*v repeats v):
  //   0 1 2 3 4 5 6 7
endmodule

module _21_swap (
);

  main main_1 ();  // open: out_1
endmodule
