// Logisim project CPUg.circ as structural Verilog: 13 circuits, main circuit main
module main (
  input  pcreset,
  input  reset,
  input  clear
);

  wire alu_1_zero, and_1_out, clock, controller2_1_alusrc, controller2_1_bne, controller2_1_branch,
       controller2_1_memread, controller2_1_memtoreg, controller2_1_memwrite, controller2_1_regdst,
       controller2_1_regwrite, multiplexer_3_out, not_1_out, or_1_out;
  wire [1:0] controller2_1_out_11;
  wire [4:0] multiplexer_1_out;
  wire [31:0] adder_1_result, adder_2_result, alu_1_result, dm_1_dataout_32, ext_1_out_2, ifu_1_im_32,
       ifu_1_pc_address_result, multiplexer_2_out, multiplexer_4_out, multiplexer_5_out, rf_1_data2,
       rf_1_out_8, shifter_1_out;

  Clock clock_1 (.out(clock));
  IFU ifu_1 (
    .PC_ADDRESS_8(multiplexer_4_out), .pc_reset(pcreset), .IM_32(ifu_1_im_32),
    .pc_address_result(ifu_1_pc_address_result), .clock(clock));
  ADDER adder_1 (.b(32'h4), .a(ifu_1_pc_address_result), .result(adder_1_result));
  Multiplexer #(.width(5), .enable("false")) multiplexer_1 (
    .in0(ifu_1_im_32[20:16]), .in1(ifu_1_im_32[15:11]), .out(multiplexer_1_out), .sel(controller2_1_regdst));
  controller2 controller2_1 (
    .A1_5(ifu_1_im_32[31:26]), .regdst(controller2_1_regdst), .alusrc(controller2_1_alusrc),
    .memtoreg(controller2_1_memtoreg), .regwrite(controller2_1_regwrite), .memread(controller2_1_memread),
    .memwrite(controller2_1_memwrite), .branch(controller2_1_branch), .\function (ifu_1_im_32[5:0]),
    .out_11(controller2_1_out_11), .bne(controller2_1_bne));
  RF rf_1 (
    .rreg1(ifu_1_im_32[25:21]), .rreg2(ifu_1_im_32[20:16]), .data_32(multiplexer_5_out),
    .wreg_5(multiplexer_1_out), .regwrite_1(controller2_1_regwrite), .data2(rf_1_data2), .clock(clock),
    .out_8(rf_1_out_8), .reset(reset));
  EXT ext_1 (.A1_5(ifu_1_im_32[15:0]), .out_2(ext_1_out_2));
  Shifter #(.width(32)) shifter_1 (.in(ext_1_out_2), .\dist (5'b00010), .out(shifter_1_out));
  or or_1 (or_1_out, controller2_1_bne, controller2_1_branch);
  Multiplexer #(.width(32), .enable("false")) multiplexer_2 (
    .in0(rf_1_data2), .in1(ext_1_out_2), .out(multiplexer_2_out), .sel(controller2_1_alusrc));
  ADDER adder_2 (.b(adder_1_result), .a(shifter_1_out), .result(adder_2_result));
  Multiplexer #(.enable("false")) multiplexer_3 (
    .in0(alu_1_zero), .in1(not_1_out), .out(multiplexer_3_out), .sel(controller2_1_bne));
  ALU alu_1 (
    .a(rf_1_out_8), .b(multiplexer_2_out), .result(alu_1_result), .aluop_1_0(controller2_1_out_11),
    .zero(alu_1_zero));
  and and_1 (and_1_out, or_1_out, multiplexer_3_out);
  not not_1 (not_1_out, alu_1_zero);
  Multiplexer #(.width(32), .enable("false")) multiplexer_4 (
    .in0(adder_1_result), .in1(adder_2_result), .out(multiplexer_4_out), .sel(and_1_out));
  DM dm_1 (
    .address_5(alu_1_result[6:2]), .datain_32(rf_1_data2), .dataout_32(dm_1_dataout_32),
    .memorywrite(controller2_1_memwrite), .memoryread(controller2_1_memread), .clock(clock), .clear(clear));
  Multiplexer #(.width(32), .enable("false")) multiplexer_5 (
    .in0(alu_1_result), .in1(dm_1_dataout_32), .out(multiplexer_5_out), .sel(controller2_1_memtoreg));
endmodule

module IFU (
  input  [31:0] PC_ADDRESS_8,
  input  clock,
  input  pc_reset,
  output [31:0] pc_address_result,
  output [31:0] IM_32
);

  Register #(.width(32)) PC (.D(PC_ADDRESS_8), .Q(pc_address_result), .clk(clock), .clr(pc_reset));  // open: en
  ROM #(.addrWidth(5), .dataWidth(32)) rom_1 (.addr(pc_address_result[6:2]), .data(IM_32));  // open: sel

  // Notes on the sheet:
  //   contents of rom_1 (hex, n*v repeats v):
  //   0 34010001 34020008 34100000 34110008 3c12aabb 12200009 ae120000 8e130000 2619821 ae130004 2619821
  //   2609021 2028021 2218823 1620fff6 21
endmodule

module RF (
  input  [4:0] rreg1,
  input  [4:0] rreg2,
  input  [31:0] data_32,
  input  reset,
  input  [4:0] wreg_5,
  input  regwrite_1,
  input  clock,
  output [31:0] out_8,
  output [31:0] data2
);

  wire decoder_1_out0, decoder_1_out1, decoder_1_out2, decoder_1_out3, decoder_1_out4, decoder_1_out5,
       decoder_1_out6, decoder_1_out7, decoder_1_out8, decoder_1_out9, decoder_1_out10, decoder_1_out11,
       decoder_1_out12, decoder_1_out13, decoder_1_out14, decoder_1_out15, decoder_1_out16, decoder_1_out17,
       decoder_1_out18, decoder_1_out19, decoder_1_out20, decoder_1_out21, decoder_1_out22, decoder_1_out23,
       decoder_1_out24, decoder_1_out25, decoder_1_out26, decoder_1_out27, decoder_1_out28, decoder_1_out29,
       decoder_1_out30, decoder_1_out31;
  wire [31:0] regslt_1_data_32_2, regslt_2_data_32_2, regslt_3_data_32_2, regslt_4_data_32_2,
       regslt_5_data_32_2, regslt_6_data_32_2, regslt_7_data_32_2, regslt_8_data_32_2, regslt_9_data_32_2,
       regslt_10_data_32_2, regslt_11_data_32_2, regslt_12_data_32_2, regslt_13_data_32_2,
       regslt_14_data_32_2, regslt_15_data_32_2, regslt_16_data_32_2, regslt_17_data_32_2,
       regslt_18_data_32_2, regslt_19_data_32_2, regslt_20_data_32_2, regslt_21_data_32_2,
       regslt_22_data_32_2, regslt_23_data_32_2, regslt_24_data_32_2, regslt_25_data_32_2,
       regslt_26_data_32_2, regslt_27_data_32_2, regslt_28_data_32_2, regslt_29_data_32_2,
       regslt_30_data_32_2, regslt_31_data_32_2, regslt_32_data_32_2;

  Decoder #(.select(5)) decoder_1 (
    .out0(decoder_1_out0), .out1(decoder_1_out1), .out2(decoder_1_out2), .out3(decoder_1_out3),
    .out4(decoder_1_out4), .out5(decoder_1_out5), .out6(decoder_1_out6), .out7(decoder_1_out7),
    .out8(decoder_1_out8), .out9(decoder_1_out9), .out10(decoder_1_out10), .out11(decoder_1_out11),
    .out12(decoder_1_out12), .out13(decoder_1_out13), .out14(decoder_1_out14), .out15(decoder_1_out15),
    .out16(decoder_1_out16), .out17(decoder_1_out17), .out18(decoder_1_out18), .out19(decoder_1_out19),
    .out20(decoder_1_out20), .out21(decoder_1_out21), .out22(decoder_1_out22), .out23(decoder_1_out23),
    .out24(decoder_1_out24), .out25(decoder_1_out25), .out26(decoder_1_out26), .out27(decoder_1_out27),
    .out28(decoder_1_out28), .out29(decoder_1_out29), .out30(decoder_1_out30), .out31(decoder_1_out31),
    .sel(wreg_5));  // open: en
  regslt regslt_1 (
    .data_32(data_32), .wreg(decoder_1_out0), .clk(clock), .regwrite(regwrite_1), .reset(reset),
    .data_32_2(regslt_1_data_32_2));
  regslt regslt_2 (
    .data_32(data_32), .wreg(decoder_1_out1), .clk(clock), .regwrite(regwrite_1), .reset(reset),
    .data_32_2(regslt_2_data_32_2));
  regslt regslt_3 (
    .data_32(data_32), .wreg(decoder_1_out2), .clk(clock), .regwrite(regwrite_1), .reset(reset),
    .data_32_2(regslt_3_data_32_2));
  regslt regslt_4 (
    .data_32(data_32), .wreg(decoder_1_out29), .clk(clock), .regwrite(regwrite_1), .reset(reset),
    .data_32_2(regslt_4_data_32_2));
  regslt regslt_5 (
    .data_32(data_32), .wreg(decoder_1_out30), .clk(clock), .regwrite(regwrite_1), .reset(reset),
    .data_32_2(regslt_5_data_32_2));
  regslt regslt_6 (
    .data_32(data_32), .wreg(decoder_1_out31), .clk(clock), .regwrite(regwrite_1), .reset(reset),
    .data_32_2(regslt_6_data_32_2));
  regslt regslt_7 (
    .data_32(data_32), .wreg(decoder_1_out3), .clk(clock), .regwrite(regwrite_1), .reset(reset),
    .data_32_2(regslt_7_data_32_2));
  regslt regslt_8 (
    .data_32(data_32), .wreg(decoder_1_out4), .clk(clock), .regwrite(regwrite_1), .reset(reset),
    .data_32_2(regslt_8_data_32_2));
  regslt regslt_9 (
    .data_32(data_32), .wreg(decoder_1_out27), .clk(clock), .regwrite(regwrite_1), .reset(reset),
    .data_32_2(regslt_9_data_32_2));
  regslt regslt_10 (
    .data_32(data_32), .wreg(decoder_1_out28), .clk(clock), .regwrite(regwrite_1), .reset(reset),
    .data_32_2(regslt_10_data_32_2));
  regslt regslt_11 (
    .data_32(data_32), .wreg(decoder_1_out5), .clk(clock), .regwrite(regwrite_1), .reset(reset),
    .data_32_2(regslt_11_data_32_2));
  regslt regslt_12 (
    .data_32(data_32), .wreg(decoder_1_out6), .clk(clock), .regwrite(regwrite_1), .reset(reset),
    .data_32_2(regslt_12_data_32_2));
  regslt regslt_13 (
    .data_32(data_32), .wreg(decoder_1_out7), .clk(clock), .regwrite(regwrite_1), .reset(reset),
    .data_32_2(regslt_13_data_32_2));
  regslt regslt_14 (
    .data_32(data_32), .wreg(decoder_1_out24), .clk(clock), .regwrite(regwrite_1), .reset(reset),
    .data_32_2(regslt_14_data_32_2));
  regslt regslt_15 (
    .data_32(data_32), .wreg(decoder_1_out25), .clk(clock), .regwrite(regwrite_1), .reset(reset),
    .data_32_2(regslt_15_data_32_2));
  regslt regslt_16 (
    .data_32(data_32), .wreg(decoder_1_out26), .clk(clock), .regwrite(regwrite_1), .reset(reset),
    .data_32_2(regslt_16_data_32_2));
  regslt regslt_17 (
    .data_32(data_32), .wreg(decoder_1_out8), .clk(clock), .regwrite(regwrite_1), .reset(reset),
    .data_32_2(regslt_17_data_32_2));
  regslt regslt_18 (
    .data_32(data_32), .wreg(decoder_1_out9), .clk(clock), .regwrite(regwrite_1), .reset(reset),
    .data_32_2(regslt_18_data_32_2));
  regslt regslt_19 (
    .data_32(data_32), .wreg(decoder_1_out10), .clk(clock), .regwrite(regwrite_1), .reset(reset),
    .data_32_2(regslt_19_data_32_2));
  regslt regslt_20 (
    .data_32(data_32), .wreg(decoder_1_out21), .clk(clock), .regwrite(regwrite_1), .reset(reset),
    .data_32_2(regslt_20_data_32_2));
  regslt regslt_21 (
    .data_32(data_32), .wreg(decoder_1_out22), .clk(clock), .regwrite(regwrite_1), .reset(reset),
    .data_32_2(regslt_21_data_32_2));
  regslt regslt_22 (
    .data_32(data_32), .wreg(decoder_1_out23), .clk(clock), .regwrite(regwrite_1), .reset(reset),
    .data_32_2(regslt_22_data_32_2));
  regslt regslt_23 (
    .data_32(data_32), .wreg(decoder_1_out11), .clk(clock), .regwrite(regwrite_1), .reset(reset),
    .data_32_2(regslt_23_data_32_2));
  regslt regslt_24 (
    .data_32(data_32), .wreg(decoder_1_out12), .clk(clock), .regwrite(regwrite_1), .reset(reset),
    .data_32_2(regslt_24_data_32_2));
  regslt regslt_25 (
    .data_32(data_32), .wreg(decoder_1_out19), .clk(clock), .regwrite(regwrite_1), .reset(reset),
    .data_32_2(regslt_25_data_32_2));
  regslt regslt_26 (
    .data_32(data_32), .wreg(decoder_1_out20), .clk(clock), .regwrite(regwrite_1), .reset(reset),
    .data_32_2(regslt_26_data_32_2));
  regslt regslt_27 (
    .data_32(data_32), .wreg(decoder_1_out13), .clk(clock), .regwrite(regwrite_1), .reset(reset),
    .data_32_2(regslt_27_data_32_2));
  regslt regslt_28 (
    .data_32(data_32), .wreg(decoder_1_out14), .clk(clock), .regwrite(regwrite_1), .reset(reset),
    .data_32_2(regslt_28_data_32_2));
  regslt regslt_29 (
    .data_32(data_32), .wreg(decoder_1_out15), .clk(clock), .regwrite(regwrite_1), .reset(reset),
    .data_32_2(regslt_29_data_32_2));
  regslt regslt_30 (
    .data_32(data_32), .wreg(decoder_1_out16), .clk(clock), .regwrite(regwrite_1), .reset(reset),
    .data_32_2(regslt_30_data_32_2));
  regslt regslt_31 (
    .data_32(data_32), .wreg(decoder_1_out17), .clk(clock), .regwrite(regwrite_1), .reset(reset),
    .data_32_2(regslt_31_data_32_2));
  regslt regslt_32 (
    .data_32(data_32), .wreg(decoder_1_out18), .clk(clock), .regwrite(regwrite_1), .reset(reset),
    .data_32_2(regslt_32_data_32_2));
  Multiplexer #(.select(5), .width(32)) multiplexer_1 (
    .in0(regslt_1_data_32_2), .in1(regslt_2_data_32_2), .in2(regslt_3_data_32_2), .in3(regslt_7_data_32_2),
    .in4(regslt_8_data_32_2), .in5(regslt_11_data_32_2), .in6(regslt_12_data_32_2),
    .in7(regslt_13_data_32_2), .in8(regslt_17_data_32_2), .in9(regslt_18_data_32_2),
    .in10(regslt_19_data_32_2), .in11(regslt_23_data_32_2), .in12(regslt_24_data_32_2),
    .in13(regslt_27_data_32_2), .in14(regslt_28_data_32_2), .in15(regslt_29_data_32_2),
    .in16(regslt_30_data_32_2), .in17(regslt_31_data_32_2), .in18(regslt_32_data_32_2),
    .in19(regslt_25_data_32_2), .in20(regslt_26_data_32_2), .in21(regslt_20_data_32_2),
    .in22(regslt_21_data_32_2), .in23(regslt_22_data_32_2), .in24(regslt_14_data_32_2),
    .in25(regslt_15_data_32_2), .in26(regslt_16_data_32_2), .in27(regslt_9_data_32_2),
    .in28(regslt_10_data_32_2), .in29(regslt_4_data_32_2), .in30(regslt_5_data_32_2),
    .in31(regslt_6_data_32_2), .out(out_8), .sel(rreg1));  // open: en
  Multiplexer #(.select(5), .width(32)) multiplexer_2 (
    .in0(regslt_1_data_32_2), .in1(regslt_2_data_32_2), .in2(regslt_3_data_32_2), .in3(regslt_7_data_32_2),
    .in4(regslt_8_data_32_2), .in5(regslt_11_data_32_2), .in6(regslt_12_data_32_2),
    .in7(regslt_13_data_32_2), .in8(regslt_17_data_32_2), .in9(regslt_18_data_32_2),
    .in10(regslt_19_data_32_2), .in11(regslt_23_data_32_2), .in12(regslt_24_data_32_2),
    .in13(regslt_27_data_32_2), .in14(regslt_28_data_32_2), .in15(regslt_29_data_32_2),
    .in16(regslt_30_data_32_2), .in17(regslt_31_data_32_2), .in18(regslt_32_data_32_2),
    .in19(regslt_25_data_32_2), .in20(regslt_26_data_32_2), .in21(regslt_20_data_32_2),
    .in22(regslt_21_data_32_2), .in23(regslt_22_data_32_2), .in24(regslt_14_data_32_2),
    .in25(regslt_15_data_32_2), .in26(regslt_16_data_32_2), .in27(regslt_9_data_32_2),
    .in28(regslt_10_data_32_2), .in29(regslt_4_data_32_2), .in30(regslt_5_data_32_2),
    .in31(regslt_6_data_32_2), .out(data2), .sel(rreg2));  // open: en
endmodule

// ctroller
module controller2 (
  input  [5:0] A1_5,
  input  [5:0] \function ,
  output regdst,
  output alusrc,
  output memtoreg,
  output regwrite,
  output memread,
  output memwrite,
  output branch,
  output bne,
  output [1:0] out_11
);

  wire addu_out, lui_out, not_1_out, not_2_out, not_3_out, not_4_out, not_5_out, not_6_out, not_7_out,
       or_3_out, or_4_out, ori_out, subu_out;

  not not_1 (not_1_out, A1_5[3]);
  not not_2 (not_2_out, A1_5[4]);
  not not_3 (not_3_out, A1_5[2]);
  not not_4 (not_4_out, A1_5[5]);
  not not_5 (not_5_out, A1_5[0]);
  not not_6 (not_6_out, A1_5[1]);
  and r_format (regdst, not_4_out, not_2_out, not_1_out, not_3_out, not_6_out, not_5_out);
  and lw (memread, A1_5[5], not_2_out, not_1_out, not_3_out, A1_5[1], A1_5[0]);
  and sw (memwrite, A1_5[5], not_2_out, A1_5[3], not_3_out, A1_5[1], A1_5[0]);
  and beq (branch, not_4_out, not_2_out, not_1_out, A1_5[2], not_6_out, not_5_out);
  and lui (lui_out, not_4_out, not_2_out, A1_5[3], A1_5[2], A1_5[1], A1_5[0]);
  and ori (ori_out, not_4_out, not_2_out, A1_5[3], A1_5[2], not_6_out, A1_5[0]);
  and u_bne (bne, not_4_out, not_2_out, not_1_out, A1_5[2], not_6_out, A1_5[0]);
  or or_1 (alusrc, memread, ori_out, lui_out, memwrite);
  or or_2 (regwrite, memread, lui_out, ori_out, regdst);
  and subu (subu_out, regdst, \function [1]);
  or or_3 (or_3_out, subu_out, bne, branch);
  not not_7 (not_7_out, \function [1]);
  and addu (addu_out, regdst, not_7_out);
  or or_4 (or_4_out, addu_out, memread, memwrite);
  coder coder_1 (.a3(lui_out), .a2(ori_out), .a1(or_3_out), .a0(or_4_out), .op1(out_11[1]), .op0(out_11[0]));

  assign memtoreg = memread;
endmodule

module ALU (
  input  [31:0] a,
  input  [31:0] b,
  input  [1:0] aluop_1_0,
  output zero,
  output [31:0] result
);

  wire or_2_out;
  wire [31:0] adder_1_result, adder_2_result, adder_3_result, not_1_out, or_1_out, shifter_1_out;

  assign not_1_out = ~b;  // NOT_Gate not_1, 32 bits wide
  ADDER adder_1 (.b(a), .a(b), .result(adder_1_result));
  ADDER adder_2 (.b(32'h1), .a(not_1_out), .result(adder_2_result));
  assign or_1_out = b | a;  // OR_Gate or_1, 32 bits wide
  Shifter #(.width(32)) shifter_1 (.in(b), .\dist (5'b10000), .out(shifter_1_out));
  ADDER adder_3 (.b(a), .a(adder_2_result), .result(adder_3_result));
  or or_2 (or_2_out, result[0], result[1], result[2], result[3], result[4], result[5], result[6], result[7], result[8], result[9], result[10], result[11], result[12], result[13], result[14], result[15], result[16], result[17], result[18], result[19], result[20], result[21], result[22], result[23], result[24], result[25], result[26], result[27], result[28], result[29], result[30], result[31]);
  Multiplexer #(.select(2), .width(32), .enable("false")) multiplexer_1 (
    .in0(adder_1_result), .in1(adder_3_result), .in2(or_1_out), .in3(shifter_1_out), .out(result),
    .sel(aluop_1_0));
  not not_2 (zero, or_2_out);

  // Notes on the sheet:
  //   00_加法
  //   01_减法
  //   10_或
  //   11_左移
endmodule

module DM (
  input  [4:0] address_5,
  input  [31:0] datain_32,
  input  memorywrite,
  input  clock,
  input  memoryread,
  input  clear,
  output [31:0] dataout_32
);

  RAM #(.addrWidth(5), .dataWidth(32), .bus("separate")) ram_1 (
    .addr(address_5), .din(datain_32), .data(dataout_32), .str(memorywrite), .clk(clock), .ld(memoryread),
    .clr(clear));  // open: sel
endmodule

module EXT (
  input  [15:0] A1_5,
  output [31:0] out_2
);


  assign out_2 = {{17{A1_5[15]}}, A1_5[14:0]};
endmodule

// ADD
module ADDER (
  input  [31:0] b,
  input  [31:0] a,
  output [31:0] result
);

  wire adder_8_1_cout, adder_8_3_cout, adder_8_4_cout, adder_8_5_cout, adder_8_6_cout, adder_8_7_cout,
       adder_8_8_cout;

  ADDER_8 adder_8_1 (.cout(adder_8_1_cout), .b(b[27:24]), .a(a[27:24]), .cin(adder_8_3_cout), .s(result[27:24]));
  ADDER_8 adder_8_2 (.b(b[31:28]), .a(a[31:28]), .cin(adder_8_1_cout), .s(result[31:28]));  // open: cout
  ADDER_8 adder_8_3 (.cout(adder_8_3_cout), .b(b[23:20]), .a(a[23:20]), .cin(adder_8_4_cout), .s(result[23:20]));
  ADDER_8 adder_8_4 (.cout(adder_8_4_cout), .b(b[19:16]), .a(a[19:16]), .cin(adder_8_5_cout), .s(result[19:16]));
  ADDER_8 adder_8_5 (.cout(adder_8_5_cout), .b(b[15:12]), .a(a[15:12]), .cin(adder_8_6_cout), .s(result[15:12]));
  ADDER_8 adder_8_6 (.cout(adder_8_6_cout), .b(b[11:8]), .a(a[11:8]), .cin(adder_8_7_cout), .s(result[11:8]));
  ADDER_8 adder_8_7 (.cout(adder_8_7_cout), .b(b[7:4]), .a(a[7:4]), .cin(adder_8_8_cout), .s(result[7:4]));
  ADDER_8 adder_8_8 (.cout(adder_8_8_cout), .b(b[3:0]), .a(a[3:0]), .cin(1'b0), .s(result[3:0]));
endmodule

module ADDER_8 (
  input  [3:0] b,
  input  [3:0] a,
  input  cin,
  output cout,
  output [3:0] s
);

  wire adder_8_4_2_cout, adder_8_4_3_cout, adder_8_4_4_cout;

  adder_8_4 adder_8_4_1 (.cin(adder_8_4_2_cout), .d1(a[3]), .d2(b[3]), .cout(cout), .s(s[3]));
  adder_8_4 adder_8_4_2 (.cin(adder_8_4_3_cout), .d1(a[2]), .d2(b[2]), .cout(adder_8_4_2_cout), .s(s[2]));
  adder_8_4 adder_8_4_3 (.cin(adder_8_4_4_cout), .d1(a[1]), .d2(b[1]), .cout(adder_8_4_3_cout), .s(s[1]));
  adder_8_4 adder_8_4_4 (.cin(cin), .d1(a[0]), .d2(b[0]), .cout(adder_8_4_4_cout), .s(s[0]));
endmodule

module adder_8_4 (
  input  cin,
  input  d1,
  input  d2,
  output cout,
  output s
);

  wire and_1_out, and_2_out, and_3_out, and_4_out, and_5_out, and_6_out, and_7_out, not_1_out, not_2_out,
       not_3_out, not_4_out, not_5_out, not_6_out;

  and and_1 (and_1_out, d1, d2);
  and and_2 (and_2_out, cin, d2);
  and and_3 (and_3_out, cin, d1);
  not not_1 (not_1_out, cin);
  not not_2 (not_2_out, d1);
  not not_3 (not_3_out, cin);
  not not_4 (not_4_out, d2);
  not not_5 (not_5_out, d1);
  not not_6 (not_6_out, d2);
  or or_1 (cout, and_1_out, and_2_out, and_3_out);
  and and_4 (and_4_out, not_1_out, not_2_out, d2);
  and and_5 (and_5_out, not_3_out, d1, not_4_out);
  and and_6 (and_6_out, cin, not_5_out, not_6_out);
  and and_7 (and_7_out, cin, d1, d2);
  or or_2 (s, and_4_out, and_5_out, and_6_out, and_7_out);
endmodule

module regslt (
  input  [31:0] data_32,
  input  wreg,
  input  clk,
  input  regwrite,
  input  reset,
  output [31:0] data_32_2
);

  wire and_1_out;

  and and_1 (and_1_out, wreg, regwrite);
  Register #(.width(32)) register_1 (.D(data_32), .en(and_1_out), .Q(data_32_2), .clk(clk), .clr(reset));
endmodule

module aluctrl (
  input  [3:0] A1_5,
  input  [5:0] fuction,
  output [1:0] out_3
);

  wire and_1_out, not_1_out, not_2_out, not_3_out;

  not not_1 (not_1_out, A1_5[3]);
  not not_2 (not_2_out, A1_5[1]);
  not not_3 (not_3_out, A1_5[0]);
  and and_1 (and_1_out, A1_5[1], fuction[1]);
  and and_2 (out_3[1], not_1_out, not_2_out, not_3_out);
  or or_1 (out_3[0], A1_5[0], and_1_out, A1_5[2]);
endmodule

module coder (
  input  a3,
  input  a2,
  input  a1,
  input  a0,
  output op1,
  output op0
);

  wire not_1_out, not_2_out, not_3_out, not_4_out;

  not not_1 (not_1_out, a1);
  and and_1 (op1, not_1_out, not_2_out);
  not not_2 (not_2_out, a0);
  not not_3 (not_3_out, a2);
  and and_2 (op0, not_3_out, not_4_out);
  not not_4 (not_4_out, a0);
endmodule
