// Logisim project cpu - blez.circ as structural Verilog: 9 circuits, main circuit main
module main (
  input  Reset
);

  wire alu_1_blez, alu_1_zero, and_1_out, clk, control_1_alusrc, control_1_branch, control_1_memtoreg,
       control_1_memwrite, control_1_regdst, control_1_regwrite, control_1_shift, or_1_out, PCsrc_out;
  wire [2:0] control_1_aluctr_2_0;
  wire [4:0] multiplexer_3_out;
  wire [29:0] ifu_1_out_4, multiplexer_1_out, n32add_1_result;
  wire [31:0] alu_1_result, bit_extender_1_out, dm_1_rd, gpr_1_rdata1, gpr_1_rdata2, ifu_1_opcode,
       multiplexer_2_out, multiplexer_4_out, multiplexer_5_out, multiplexer_6_out, shifter_1_out;
  wire [31:30] ifu_1_out_4_2, n32add_1_result_2;

  Multiplexer #(.width(30)) multiplexer_1 (
    .in0(ifu_1_out_4), .in1(n32add_1_result), .out(multiplexer_1_out), .sel(or_1_out));  // open: en
  Clock clock_1 (.out(clk));
  IFU ifu_1 (
    .PCnext(multiplexer_1_out), .Reset(Reset), .OPcode(ifu_1_opcode), .out_4({ifu_1_out_4_2, ifu_1_out_4}));  // open: Cout
  assign bit_extender_1_out = {{16{1'b0}}, ifu_1_opcode[15:0]};  // Bit_Extender bit_extender_1
  Control control_1 (
    .opcode(ifu_1_opcode[31:26]), .funt(ifu_1_opcode[5:0]), .RegDst(control_1_regdst),
    .ALUSrc(control_1_alusrc), .MemtoReg(control_1_memtoreg), .RegWrite(control_1_regwrite),
    .MemWrite(control_1_memwrite), .Branch(control_1_branch), .shift(control_1_shift),
    .ALUctr_2_0(control_1_aluctr_2_0));
  GPR gpr_1 (
    .Wdata(multiplexer_6_out), .clk(clk), .RegWrite(control_1_regwrite), .Wreg(multiplexer_3_out),
    .reg1(ifu_1_opcode[25:21]), .reg2(ifu_1_opcode[20:16]), .Rdata1(gpr_1_rdata1), .Rdata2(gpr_1_rdata2));
  Shifter #(.width(32)) shifter_1 (.in(bit_extender_1_out), .\dist (5'b10000), .out(shifter_1_out));
  Multiplexer #(.width(32)) multiplexer_2 (
    .in0(gpr_1_rdata2), .in1(multiplexer_4_out), .out(multiplexer_2_out), .sel(control_1_alusrc));  // open: en
  Multiplexer #(.width(5)) multiplexer_3 (
    .in0(ifu_1_opcode[20:16]), .in1(ifu_1_opcode[15:11]), .out(multiplexer_3_out), .sel(control_1_regdst));  // open: en
  Multiplexer #(.width(32)) multiplexer_4 (
    .in0(bit_extender_1_out), .in1(shifter_1_out), .out(multiplexer_4_out), .sel(control_1_shift));  // open: en
  ALU alu_1 (
    .SrcA(gpr_1_rdata1), .SrcB(multiplexer_2_out), .blez(alu_1_blez), .ALUcontrol(control_1_aluctr_2_0),
    .Zero(alu_1_zero), .Result(alu_1_result));  // open: Cout
  _32ADD u_32add_1 (
    .SrcA(multiplexer_4_out), .Cin(1'b0), .SrcB({ifu_1_out_4_2, ifu_1_out_4}),
    .Result({n32add_1_result_2, n32add_1_result}));  // open: Cout
  DM dm_1 (.A(alu_1_result), .Wdata(gpr_1_rdata2), .MemWrite(control_1_memwrite), .RD(dm_1_rd));  // open: Memread
  Multiplexer #(.width(32)) multiplexer_5 (
    .in0(alu_1_result), .in1(dm_1_rd), .out(multiplexer_5_out), .sel(control_1_memtoreg));  // open: en
  Multiplexer #(.width(32)) multiplexer_6 (
    .in0(multiplexer_5_out), .in1(multiplexer_4_out), .out(multiplexer_6_out), .sel(control_1_shift));  // open: en
  and PCsrc (PCsrc_out, control_1_branch, alu_1_zero);
  or or_1 (or_1_out, PCsrc_out, and_1_out);
  and and_1 (and_1_out, control_1_branch, alu_1_blez);
endmodule

module ALU (
  input  [31:0] SrcA,
  input  [31:0] SrcB,
  input  [2:0] ALUcontrol,
  output Cout,
  output Zero,
  output [31:0] Result,
  output blez
);

  wire or_2_out, undriven_2;
  wire [31:0] and_1_out, multiplexer_1_out, n32add_1_result, not_1_out, or_1_out, undriven;

  assign not_1_out = ~SrcB;  // NOT_Gate not_1, 32 bits wide
  Multiplexer #(.width(32)) multiplexer_1 (
    .in0(SrcB), .in1(not_1_out), .out(multiplexer_1_out), .sel(ALUcontrol[2]));  // open: en
  assign and_1_out = SrcA & multiplexer_1_out;  // AND_Gate and_1, 32 bits wide
  assign or_1_out = SrcA | multiplexer_1_out;  // OR_Gate or_1, 32 bits wide
  _32ADD u_32add_1 (.SrcA(SrcA), .Cin(ALUcontrol[2]), .SrcB(multiplexer_1_out), .Cout(Cout), .Result(n32add_1_result));
  Multiplexer #(.select(2), .width(32)) multiplexer_2 (
    .in0(and_1_out), .in1(or_1_out), .in2(n32add_1_result), .in3(undriven), .out(Result),
    .sel(ALUcontrol[1:0]));  // open: en
  or or_2 (or_2_out, Result[0], Result[1], Result[2], Result[3], Result[4], Result[5], Result[6], Result[7], Result[8], Result[9], Result[10], Result[11], Result[12], Result[13], Result[14], Result[15], Result[16], Result[17], Result[18], Result[19], Result[20], Result[21], Result[22], Result[23], Result[24], Result[25], Result[26], Result[27], Result[28], Result[29], Result[30], Result[31]);
  not not_2 (Zero, or_2_out);
  // Probe on undriven_2

  assign blez = SrcA[31];
endmodule

module _1add (
  input  C_in,
  input  Src_A,
  input  Src_B,
  output C_out,
  output Result
);

  wire and_1_out, and_2_out, and_3_out, and_4_out, and_5_out, and_6_out, and_7_out, not_1_out, not_2_out,
       not_3_out, not_4_out, not_5_out, not_6_out;

  and and_1 (and_1_out, Src_A, Src_B);
  and and_2 (and_2_out, C_in, Src_B);
  and and_3 (and_3_out, C_in, Src_A);
  not not_1 (not_1_out, C_in);
  not not_2 (not_2_out, Src_A);
  not not_3 (not_3_out, C_in);
  not not_4 (not_4_out, Src_B);
  not not_5 (not_5_out, Src_A);
  not not_6 (not_6_out, Src_B);
  or or_1 (C_out, and_1_out, and_2_out, and_3_out);
  and and_4 (and_4_out, not_1_out, not_2_out, Src_B);
  and and_5 (and_5_out, not_3_out, Src_A, not_4_out);
  and and_6 (and_6_out, C_in, not_5_out, not_6_out);
  and and_7 (and_7_out, C_in, Src_A, Src_B);
  or or_2 (Result, and_4_out, and_5_out, and_6_out, and_7_out);
endmodule

module _32ADD (
  input  [31:0] SrcA,
  input  Cin,
  input  [31:0] SrcB,
  output [31:0] Result,
  output Cout
);

  wire n8add_1_cout, n8add_2_cout, n8add_3_cout;

  _8ADD u_8add_1 (.SrcA(SrcA[7:0]), .SrcB(SrcB[7:0]), .Cin(Cin), .Cout(n8add_1_cout), .Rsult(Result[7:0]));
  _8ADD u_8add_2 (
    .SrcA(SrcA[23:16]), .SrcB(SrcB[23:16]), .Cin(n8add_3_cout), .Cout(n8add_2_cout), .Rsult(Result[23:16]));
  _8ADD u_8add_3 (.SrcA(SrcA[15:8]), .SrcB(SrcB[15:8]), .Cin(n8add_1_cout), .Cout(n8add_3_cout), .Rsult(Result[15:8]));
  _8ADD u_8add_4 (.SrcA(SrcA[31:24]), .SrcB(SrcB[31:24]), .Cin(n8add_2_cout), .Cout(Cout), .Rsult(Result[31:24]));
endmodule

module _8ADD (
  input  Cin,
  input  [7:0] SrcA,
  input  [7:0] SrcB,
  output [7:0] Rsult,
  output Cout
);

  wire n1add_1_c_out, n1add_2_c_out, n1add_3_c_out, n1add_4_c_out, n1add_5_c_out, n1add_6_c_out,
       n1add_7_c_out;

  _1add u_1add_1 (.C_in(Cin), .Src_A(SrcA[0]), .Src_B(SrcB[0]), .C_out(n1add_1_c_out), .Result(Rsult[0]));
  _1add u_1add_2 (.C_in(n1add_7_c_out), .Src_A(SrcA[4]), .Src_B(SrcB[4]), .C_out(n1add_2_c_out), .Result(Rsult[4]));
  _1add u_1add_3 (.C_in(n1add_1_c_out), .Src_A(SrcA[1]), .Src_B(SrcB[1]), .C_out(n1add_3_c_out), .Result(Rsult[1]));
  _1add u_1add_4 (.C_in(n1add_2_c_out), .Src_A(SrcA[5]), .Src_B(SrcB[5]), .C_out(n1add_4_c_out), .Result(Rsult[5]));
  _1add u_1add_5 (.C_in(n1add_3_c_out), .Src_A(SrcA[2]), .Src_B(SrcB[2]), .C_out(n1add_5_c_out), .Result(Rsult[2]));
  _1add u_1add_6 (.C_in(n1add_4_c_out), .Src_A(SrcA[6]), .Src_B(SrcB[6]), .C_out(n1add_6_c_out), .Result(Rsult[6]));
  _1add u_1add_7 (.C_in(n1add_5_c_out), .Src_A(SrcA[3]), .Src_B(SrcB[3]), .C_out(n1add_7_c_out), .Result(Rsult[3]));
  _1add u_1add_8 (.C_in(n1add_6_c_out), .Src_A(SrcA[7]), .Src_B(SrcB[7]), .C_out(Cout), .Result(Rsult[7]));
endmodule

module IFU (
  input  [29:0] PCnext,
  input  Reset,
  output [31:0] OPcode,
  output [31:0] out_4,
  output Cout
);

  wire clk, not_1_out;
  wire [29:0] register_1_q;

  Clock clock_1 (.out(clk));
  Register #(.width(30)) register_1 (.D(PCnext), .Q(register_1_q), .clk(not_1_out), .clr(Reset));  // open: en
  not not_1 (not_1_out, clk);
  _32ADD u_32add_1 (.SrcA({2'b00, register_1_q}), .Cin(1'b0), .SrcB(32'h1), .Cout(Cout), .Result(out_4));
  ROM #(.addrWidth(5), .dataWidth(32)) rom_1 (.addr(register_1_q[4:0]), .data(OPcode));  // open: sel

  // Notes on the sheet:
  //   contents of rom_1 (hex, n*v repeats v):
  //   3401000a 3402000b 11821 22021 202823 403023 643821 834023 3c09000a ac01000c 8c0a000c 340b0001
  //   340c000a 340d0000 340e0000 1ab6821 1cd7021 18b6023 11800001 1000fffb ac0e0010
endmodule

module GPR (
  input  [4:0] reg1,
  input  [4:0] Wreg,
  input  [4:0] reg2,
  input  [31:0] Wdata,
  input  clk,
  input  RegWrite,
  output [31:0] Rdata1,
  output [31:0] Rdata2
);

  wire and_1_out, and_2_out, and_3_out, and_4_out, and_5_out, and_6_out, and_7_out, and_8_out, and_9_out,
       and_10_out, and_11_out, and_12_out, and_13_out, and_14_out, and_15_out, and_16_out, and_17_out,
       and_18_out, and_19_out, and_20_out, and_21_out, and_22_out, and_23_out, and_24_out, and_25_out,
       and_26_out, and_27_out, and_28_out, and_29_out, and_30_out, and_31_out, and_32_out, decoder_1_out0,
       decoder_1_out1, decoder_1_out2, decoder_1_out3, decoder_1_out4, decoder_1_out5, decoder_1_out6,
       decoder_1_out7, decoder_1_out8, decoder_1_out9, decoder_1_out10, decoder_1_out11, decoder_1_out12,
       decoder_1_out13, decoder_1_out14, decoder_1_out15, decoder_1_out16, decoder_1_out17, decoder_1_out18,
       decoder_1_out19, decoder_1_out20, decoder_1_out21, decoder_1_out22, decoder_1_out23, decoder_1_out24,
       decoder_1_out25, decoder_1_out26, decoder_1_out27, decoder_1_out28, decoder_1_out29, decoder_1_out30,
       decoder_1_out31;
  wire [31:0] register_1_q, register_2_q, register_3_q, register_4_q, register_5_q, register_6_q,
       register_7_q, register_8_q, register_9_q, register_10_q, register_11_q, register_12_q, register_13_q,
       register_14_q, register_15_q, register_16_q, register_17_q, register_18_q, register_19_q,
       register_20_q, register_21_q, register_22_q, register_23_q, register_24_q, register_25_q,
       register_26_q, register_27_q, register_28_q, register_29_q, register_30_q, register_31_q,
       register_32_q;

  Decoder #(.select(5)) decoder_1 (
    .out0(decoder_1_out0), .out1(decoder_1_out1), .out2(decoder_1_out2), .out3(decoder_1_out3),
    .out4(decoder_1_out4), .out5(decoder_1_out5), .out6(decoder_1_out6), .out7(decoder_1_out7),
    .out8(decoder_1_out8), .out9(decoder_1_out9), .out10(decoder_1_out10), .out11(decoder_1_out11),
    .out12(decoder_1_out12), .out13(decoder_1_out13), .out14(decoder_1_out14), .out15(decoder_1_out15),
    .out16(decoder_1_out16), .out17(decoder_1_out17), .out18(decoder_1_out18), .out19(decoder_1_out19),
    .out20(decoder_1_out20), .out21(decoder_1_out21), .out22(decoder_1_out22), .out23(decoder_1_out23),
    .out24(decoder_1_out24), .out25(decoder_1_out25), .out26(decoder_1_out26), .out27(decoder_1_out27),
    .out28(decoder_1_out28), .out29(decoder_1_out29), .out30(decoder_1_out30), .out31(decoder_1_out31),
    .sel(Wreg));  // open: en
  and and_1 (and_1_out, clk, decoder_1_out0, RegWrite);
  and and_2 (and_2_out, clk, decoder_1_out4, RegWrite);
  and and_3 (and_3_out, clk, decoder_1_out8, RegWrite);
  and and_4 (and_4_out, clk, decoder_1_out12, RegWrite);
  and and_5 (and_5_out, clk, decoder_1_out16, RegWrite);
  and and_6 (and_6_out, clk, decoder_1_out20, RegWrite);
  and and_7 (and_7_out, clk, decoder_1_out24, RegWrite);
  and and_8 (and_8_out, clk, decoder_1_out28, RegWrite);
  Register #(.width(32)) register_1 (.D(Wdata), .Q(register_1_q), .clk(and_1_out));  // open: en, clr
  Register #(.width(32)) register_2 (.D(Wdata), .Q(register_2_q), .clk(and_2_out));  // open: en, clr
  Register #(.width(32)) register_3 (.D(Wdata), .Q(register_3_q), .clk(and_3_out));  // open: en, clr
  Register #(.width(32)) register_4 (.D(Wdata), .Q(register_4_q), .clk(and_4_out));  // open: en, clr
  Register #(.width(32)) register_5 (.D(Wdata), .Q(register_5_q), .clk(and_5_out));  // open: en, clr
  Register #(.width(32)) register_6 (.D(Wdata), .Q(register_6_q), .clk(and_6_out));  // open: en, clr
  Register #(.width(32)) register_7 (.D(Wdata), .Q(register_7_q), .clk(and_7_out));  // open: en, clr
  Register #(.width(32)) register_8 (.D(Wdata), .Q(register_8_q), .clk(and_8_out));  // open: en, clr
  and and_9 (and_9_out, clk, decoder_1_out1, RegWrite);
  and and_10 (and_10_out, clk, decoder_1_out5, RegWrite);
  and and_11 (and_11_out, clk, decoder_1_out9, RegWrite);
  and and_12 (and_12_out, clk, decoder_1_out13, RegWrite);
  and and_13 (and_13_out, clk, decoder_1_out17, RegWrite);
  and and_14 (and_14_out, clk, decoder_1_out21, RegWrite);
  and and_15 (and_15_out, clk, decoder_1_out25, RegWrite);
  and and_16 (and_16_out, clk, decoder_1_out29, RegWrite);
  Register #(.width(32)) register_9 (.D(Wdata), .Q(register_9_q), .clk(and_9_out));  // open: en, clr
  Register #(.width(32)) register_10 (.D(Wdata), .Q(register_10_q), .clk(and_10_out));  // open: en, clr
  Register #(.width(32)) register_11 (.D(Wdata), .Q(register_11_q), .clk(and_11_out));  // open: en, clr
  Register #(.width(32)) register_12 (.D(Wdata), .Q(register_12_q), .clk(and_12_out));  // open: en, clr
  Register #(.width(32)) register_13 (.D(Wdata), .Q(register_13_q), .clk(and_13_out));  // open: en, clr
  Register #(.width(32)) register_14 (.D(Wdata), .Q(register_14_q), .clk(and_14_out));  // open: en, clr
  Register #(.width(32)) register_15 (.D(Wdata), .Q(register_15_q), .clk(and_15_out));  // open: en, clr
  Register #(.width(32)) register_16 (.D(Wdata), .Q(register_16_q), .clk(and_16_out));  // open: en, clr
  and and_17 (and_17_out, clk, decoder_1_out2, RegWrite);
  and and_18 (and_18_out, clk, decoder_1_out6, RegWrite);
  and and_19 (and_19_out, clk, decoder_1_out10, RegWrite);
  and and_20 (and_20_out, clk, decoder_1_out14, RegWrite);
  and and_21 (and_21_out, clk, decoder_1_out18, RegWrite);
  and and_22 (and_22_out, clk, decoder_1_out22, RegWrite);
  and and_23 (and_23_out, clk, decoder_1_out26, RegWrite);
  and and_24 (and_24_out, clk, decoder_1_out30, RegWrite);
  Register #(.width(32)) register_17 (.D(Wdata), .Q(register_17_q), .clk(and_17_out));  // open: en, clr
  Register #(.width(32)) register_18 (.D(Wdata), .Q(register_18_q), .clk(and_18_out));  // open: en, clr
  Register #(.width(32)) register_19 (.D(Wdata), .Q(register_19_q), .clk(and_19_out));  // open: en, clr
  Register #(.width(32)) register_20 (.D(Wdata), .Q(register_20_q), .clk(and_20_out));  // open: en, clr
  Register #(.width(32)) register_21 (.D(Wdata), .Q(register_21_q), .clk(and_21_out));  // open: en, clr
  Register #(.width(32)) register_22 (.D(Wdata), .Q(register_22_q), .clk(and_22_out));  // open: en, clr
  Register #(.width(32)) register_23 (.D(Wdata), .Q(register_23_q), .clk(and_23_out));  // open: en, clr
  Register #(.width(32)) register_24 (.D(Wdata), .Q(register_24_q), .clk(and_24_out));  // open: en, clr
  and and_25 (and_25_out, clk, decoder_1_out3, RegWrite);
  and and_26 (and_26_out, clk, decoder_1_out7, RegWrite);
  and and_27 (and_27_out, clk, decoder_1_out11, RegWrite);
  and and_28 (and_28_out, clk, decoder_1_out15, RegWrite);
  and and_29 (and_29_out, clk, decoder_1_out19, RegWrite);
  and and_30 (and_30_out, clk, decoder_1_out23, RegWrite);
  and and_31 (and_31_out, clk, decoder_1_out27, RegWrite);
  and and_32 (and_32_out, clk, decoder_1_out31, RegWrite);
  Register #(.width(32)) register_25 (.D(Wdata), .Q(register_25_q), .clk(and_25_out));  // open: en, clr
  Register #(.width(32)) register_26 (.D(Wdata), .Q(register_26_q), .clk(and_26_out));  // open: en, clr
  Register #(.width(32)) register_27 (.D(Wdata), .Q(register_27_q), .clk(and_27_out));  // open: en, clr
  Register #(.width(32)) register_28 (.D(Wdata), .Q(register_28_q), .clk(and_28_out));  // open: en, clr
  Register #(.width(32)) register_29 (.D(Wdata), .Q(register_29_q), .clk(and_29_out));  // open: en, clr
  Register #(.width(32)) register_30 (.D(Wdata), .Q(register_30_q), .clk(and_30_out));  // open: en, clr
  Register #(.width(32)) register_31 (.D(Wdata), .Q(register_31_q), .clk(and_31_out));  // open: en, clr
  Register #(.width(32)) register_32 (.D(Wdata), .Q(register_32_q), .clk(and_32_out));  // open: en, clr
  Multiplexer #(.select(5), .width(32)) multiplexer_1 (
    .in0(register_1_q), .in1(register_9_q), .in2(register_17_q), .in3(register_25_q), .in4(register_2_q),
    .in5(register_10_q), .in6(register_18_q), .in7(register_26_q), .in8(register_3_q), .in9(register_11_q),
    .in10(register_19_q), .in11(register_27_q), .in12(register_4_q), .in13(register_12_q),
    .in14(register_20_q), .in15(register_28_q), .in16(register_5_q), .in17(register_13_q),
    .in18(register_21_q), .in19(register_29_q), .in20(register_6_q), .in21(register_14_q),
    .in22(register_22_q), .in23(register_30_q), .in24(register_7_q), .in25(register_15_q),
    .in26(register_23_q), .in27(register_31_q), .in28(register_8_q), .in29(register_16_q),
    .in30(register_24_q), .in31(register_32_q), .out(Rdata1), .sel(reg1));  // open: en
  Multiplexer #(.select(5), .width(32)) multiplexer_2 (
    .in0(register_1_q), .in1(register_9_q), .in2(register_17_q), .in3(register_25_q), .in4(register_2_q),
    .in5(register_10_q), .in6(register_18_q), .in7(register_26_q), .in8(register_3_q), .in9(register_11_q),
    .in10(register_19_q), .in11(register_27_q), .in12(register_4_q), .in13(register_12_q),
    .in14(register_20_q), .in15(register_28_q), .in16(register_5_q), .in17(register_13_q),
    .in18(register_21_q), .in19(register_29_q), .in20(register_6_q), .in21(register_14_q),
    .in22(register_22_q), .in23(register_30_q), .in24(register_7_q), .in25(register_15_q),
    .in26(register_23_q), .in27(register_31_q), .in28(register_8_q), .in29(register_16_q),
    .in30(register_24_q), .in31(register_32_q), .out(Rdata2), .sel(reg2));  // open: en
endmodule

module DM (
  input  [31:0] A,
  input  [31:0] Wdata,
  input  MemWrite,
  input  Memread,
  output [31:0] RD
);

  wire clk;

  Clock clock_1 (.out(clk));
  RAM #(.addrWidth(5), .dataWidth(32), .bus("separate")) ram_1 (
    .addr(A[6:2]), .din(Wdata), .data(RD), .str(MemWrite), .clk(clk), .ld(Memread));  // open: sel, clr
endmodule

// Ctr
module Control (
  input  [5:0] opcode,
  input  [5:0] funt,
  output RegDst,
  output ALUSrc,
  output MemtoReg,
  output RegWrite,
  output MemWrite,
  output Branch,
  output shift,
  output [2:0] ALUctr_2_0
);

  wire Addu_out, and_1_out, and_2_out, and_3_out, beq_out, blez_out, lui_out, lw_out, not_1_out, not_2_out,
       not_3_out, not_4_out, not_5_out, not_6_out, not_7_out, not_8_out, not_9_out, not_10_out, not_11_out,
       not_12_out, ori_out, Subu_out, sw_out;

  not not_1 (not_1_out, opcode[5]);
  not not_2 (not_2_out, funt[5]);
  not not_3 (not_3_out, opcode[4]);
  not not_4 (not_4_out, funt[3]);
  not not_5 (not_5_out, funt[4]);
  not not_6 (not_6_out, opcode[3]);
  not not_7 (not_7_out, funt[2]);
  not not_8 (not_8_out, funt[1]);
  not not_9 (not_9_out, opcode[2]);
  not not_10 (not_10_out, opcode[1]);
  not not_11 (not_11_out, funt[0]);
  not not_12 (not_12_out, opcode[0]);
  and ori (ori_out, not_1_out, not_3_out, opcode[3], opcode[2], not_10_out, opcode[0]);
  and lw (lw_out, opcode[5], not_3_out, not_6_out, not_9_out, opcode[1], opcode[0]);
  and sw (sw_out, opcode[5], not_3_out, opcode[3], not_9_out, opcode[1], opcode[0]);
  and beq (beq_out, not_1_out, not_3_out, not_6_out, opcode[2], not_10_out, not_12_out);
  and lui (lui_out, not_1_out, not_3_out, opcode[3], opcode[2], opcode[1], opcode[0]);
  and blez (blez_out, not_1_out, not_3_out, not_6_out, opcode[2], opcode[1], not_12_out);
  and and_1 (and_1_out, not_1_out, not_3_out, not_6_out, not_9_out, not_10_out, not_12_out);
  and and_2 (and_2_out, funt[5], not_5_out, not_4_out, not_7_out, funt[1], funt[0]);
  and and_3 (and_3_out, funt[5], not_5_out, not_4_out, not_7_out, not_8_out, funt[0]);
  and Addu (Addu_out, and_1_out, and_3_out);
  and Subu (Subu_out, and_1_out, and_2_out);
  or u_RegDst (RegDst, Addu_out, Subu_out);
  or u_ALUSrc (ALUSrc, ori_out, lw_out, sw_out);
  buf u_MemtoReg (MemtoReg, lw_out);  // OR_Gate
  or u_RegWrite (RegWrite, lui_out, Addu_out, Subu_out, ori_out, lw_out);
  buf u_MemWrite (MemWrite, sw_out);  // OR_Gate
  or u_Branch (Branch, beq_out, blez_out);
  buf shift16 (shift, lui_out);  // OR_Gate
  or ALUctr2 (ALUctr_2_0[2], Subu_out, beq_out);
  or ALUctr1 (ALUctr_2_0[1], beq_out, Subu_out, Addu_out, lw_out, sw_out);
  buf ALUctr0 (ALUctr_2_0[0], ori_out);  // OR_Gate
endmodule
