// Logisim project lab9ex2.circ as structural Verilog: 4 circuits, main circuit main
module main (
  input  [3:0] A,
  input  in_2,
  input  [3:0] B,
  input  [3:0] in_4,
  input  [3:0] in_5,
  input  [3:0] C,
  input  [3:0] D,
  input  [3:0] in_8,
  input  [3:0] in_9,
  output [3:0] _1,
  output [3:0] _2,
  output [3:0] out_12,
  output [3:0] out_13,
  output [3:0] _3,
  output [3:0] _4,
  output [3:0] out_16,
  output [3:0] out_17
);

  _4_bit_swap u_4_bit_swap_1 (.Input_1(in_4), .Input_2(in_5), .Output_1(out_12), .Output_2(out_13), .swap(in_2));
  _4_bit_compare___swap u_4_bit_compare_swap_1 (.Input_1(in_8), .Input_2(in_9), .Output_1(out_16), .Output_2(out_17));

  // Notes on the sheet:
  //   YOUR CIRCUIT HERE!
  //   Use this to test your swap circuit
  //   Use this to test the compare & swap element
endmodule

module _1_bit_swap (
  input  swap,
  input  Input_1,
  input  Input_2,
  output Output_1,
  output Output_2
);


  // Notes on the sheet:
  //   YOUR CIRCUIT HERE!
endmodule

module _4_bit_swap (
  input  swap,
  input  [3:0] Input_1,
  input  [3:0] Input_2,
  output [3:0] Output_1,
  output [3:0] Output_2
);

  _1_bit_swap u_1_bit_swap_1 (
    .Input_1(Input_1[0]), .Input_2(Input_2[0]), .Output_1(Output_1[0]), .Output_2(Output_2[0]), .swap(swap));
  _1_bit_swap u_1_bit_swap_2 (
    .Input_1(Input_1[1]), .Input_2(Input_2[1]), .Output_1(Output_1[1]), .Output_2(Output_2[1]), .swap(swap));
  _1_bit_swap u_1_bit_swap_3 (
    .Input_1(Input_1[2]), .Input_2(Input_2[2]), .Output_1(Output_1[2]), .Output_2(Output_2[2]), .swap(swap));
  _1_bit_swap u_1_bit_swap_4 (
    .Input_1(Input_1[3]), .Input_2(Input_2[3]), .Output_1(Output_1[3]), .Output_2(Output_2[3]), .swap(swap));
endmodule

module _4_bit_compare___swap (
  input  [3:0] Input_1,
  input  [3:0] Input_2,
  output [3:0] Output_1,
  output [3:0] Output_2
);

  wire comparator_1_gt;

  Comparator #(.width(4), .mode("unsigned")) comparator_1 (
    .a(Input_1), .b(Input_2), .gt(comparator_1_gt));  // open: eq, lt
  _4_bit_swap u_4_bit_swap_1 (
    .Input_1(Input_1), .Input_2(Input_2), .Output_1(Output_1), .Output_2(Output_2), .swap(comparator_1_gt));
endmodule
