// Logisim project mod5.circ as structural Verilog
module main (
  output out_1,
  output out_2,
  output out_3,
  output out_4,
  output out_5,
  output out_6,
  output out_7
);

  wire clock_1_out;
  wire [7:0] counter_1_q;

  Clock clock_1 (.out(clock_1_out));
  Counter counter_1 (.Q(counter_1_q), .carry(out_7), .clk(clock_1_out));  // open: load, D, count, clr
  ROM #(.dataWidth(2)) rom_1 (.addr(counter_1_q));  // open: data, sel
  mod5 mod5_1 ();
endmodule
