// Logisim project crc.circ as structural Verilog: 2 circuits, main circuit CRC
module CRC (
  input  [7:0] in_1,
  input  [3:0] in_2,
  output [10:0] out_3
);

  wire [2:0] small_1_out_3, small_2_out_3, small_3_out_3, small_4_out_3, small_5_out_3, small_6_out_3,
       small_7_out_3;

  \small  small_1 (.\被除数 (in_1[7:4]), .\除数 (in_2), .out_3(small_1_out_3));
  \small  small_2 (.\被除数 ({small_1_out_3, in_1[3]}), .\除数 (in_2), .out_3(small_2_out_3));
  \small  small_3 (.\被除数 ({small_2_out_3, in_1[2]}), .\除数 (in_2), .out_3(small_3_out_3));
  \small  small_4 (.\被除数 ({small_3_out_3, in_1[1]}), .\除数 (in_2), .out_3(small_4_out_3));
  \small  small_5 (.\被除数 ({small_4_out_3, in_1[0]}), .\除数 (in_2), .out_3(small_5_out_3));
  \small  small_6 (.\被除数 ({small_5_out_3, 1'b0}), .\除数 (in_2), .out_3(small_6_out_3));
  \small  small_7 (.\被除数 ({small_6_out_3, 1'b0}), .\除数 (in_2), .out_3(small_7_out_3));
  \small  small_8 (.\被除数 ({small_7_out_3, 1'b0}), .\除数 (in_2), .out_3(out_3[2:0]));

  assign out_3[10:3] = in_1;
endmodule

module \small  (
  input  [3:0] \被除数 ,
  input  [3:0] \除数 ,
  output [2:0] out_3
);

  wire comparator_1_eq;
  wire [2:0] xor_1_out;

  xor xor_1 (xor_1_out[0], \被除数 [0], \除数 [0]);
  xor xor_2 (xor_1_out[1], \被除数 [1], \除数 [1]);
  xor xor_3 (xor_1_out[2], \被除数 [2], \除数 [2]);
  Comparator #(.width(1), .mode("unsigned")) comparator_1 (
    .a(\被除数 [3]), .b(\除数 [3]), .eq(comparator_1_eq));  // open: gt, lt
  Multiplexer #(.width(3)) multiplexer_1 (
    .in0(\被除数 [2:0]), .in1(xor_1_out), .out(out_3), .sel(comparator_1_eq));  // open: en
endmodule
