// Logisim project fsm.circ as structural Verilog: 1 circuit, main circuit fsm
module fsm (
  input  in_1,
  input  [1:0] In,
  output out_3
);

  wire and_1_out, and_2_out, and_3_out, clock_1_out, not_1_out, not_2_out, not_3_out, not_4_out, not_5_out,
       or_1_out, register_1_q, register_2_q, register_3_q;

  not not_1 (not_1_out, In[0]);
  not not_2 (not_2_out, In[1]);
  not not_3 (not_3_out, register_2_q);
  not not_4 (not_4_out, register_3_q);
  and and_1 (and_1_out, In[0], not_2_out, not_4_out);
  and and_2 (and_2_out, not_3_out, In[0], not_2_out);
  and and_3 (and_3_out, register_2_q, not_4_out, not_1_out);
  or or_1 (or_1_out, and_1_out, and_2_out);
  Register #(.width(1)) register_1 (.D(in_1), .Q(register_1_q), .clk(clock_1_out), .clr(register_1_q));  // open: en
  Register #(.width(1)) register_2 (.D(or_1_out), .Q(register_2_q), .clk(clock_1_out), .clr(register_1_q));  // open: en
  Register #(.width(1)) register_3 (
    .D(and_3_out), .Q(register_3_q), .clk(clock_1_out), .clr(register_1_q));  // open: en
  Clock clock_1 (.out(clock_1_out));
  not not_5 (not_5_out, register_2_q);
  and and_4 (out_3, not_5_out, register_3_q, not_1_out);

  // Notes on the sheet:
  //   In0
  //   In1
  //   S0'
  //   S1'
  //   S0
  //   S1
endmodule
