// Logisim project CRC.circ as structural Verilog: 2 circuits, main circuit CRC
module CRC (
  input  [7:0] in_1,
  input  [3:0] B,
  output [10:0] out_3
);

  wire [2:0] n4bit_1_out_3, n4bit_2_out_3, n4bit_3_out_3, n4bit_4_out_3, n4bit_5_out_3, n4bit_6_out_3,
       n4bit_7_out_3;

  _4bit u_4bit_1 (.Dividend(in_1[7:4]), .Divisor(B), .out_3(n4bit_1_out_3));
  _4bit u_4bit_2 (.Dividend({n4bit_1_out_3, in_1[3]}), .Divisor(B), .out_3(n4bit_2_out_3));
  _4bit u_4bit_3 (.Dividend({n4bit_2_out_3, in_1[2]}), .Divisor(B), .out_3(n4bit_3_out_3));
  _4bit u_4bit_4 (.Dividend({n4bit_3_out_3, in_1[1]}), .Divisor(B), .out_3(n4bit_4_out_3));
  _4bit u_4bit_5 (.Dividend({n4bit_4_out_3, in_1[0]}), .Divisor(B), .out_3(n4bit_5_out_3));
  _4bit u_4bit_6 (.Dividend({n4bit_5_out_3, 1'b0}), .Divisor(B), .out_3(n4bit_6_out_3));
  _4bit u_4bit_7 (.Dividend({n4bit_6_out_3, 1'b0}), .Divisor(B), .out_3(n4bit_7_out_3));
  _4bit u_4bit_8 (.Dividend({n4bit_7_out_3, 1'b0}), .Divisor(B), .out_3(out_3[2:0]));

  assign out_3[10:3] = in_1;

  // Notes on the sheet:
  //   A
endmodule

module _4bit (
  input  [3:0] Dividend,
  input  [3:0] Divisor,
  output [2:0] out_3
);

  wire comparator_1_eq, multiplexer_1_out;
  wire [2:0] xor_1_out;

  xor xor_1 (xor_1_out[0], Divisor[0], Dividend[0]);
  xor xor_2 (xor_1_out[1], Divisor[1], Dividend[1]);
  xor xor_3 (xor_1_out[2], Divisor[2], Dividend[2]);
  Comparator #(.width(1)) comparator_1 (.a(Dividend[3]), .b(Divisor[3]), .eq(comparator_1_eq));  // open: gt, lt
  Multiplexer multiplexer_1 (.in0(1'b0), .in1(1'b1), .out(multiplexer_1_out), .sel(comparator_1_eq));  // open: en
  Multiplexer #(.width(3)) multiplexer_2 (
    .in0(Dividend[2:0]), .in1(xor_1_out), .out(out_3), .sel(multiplexer_1_out));  // open: en

  // Notes on the sheet:
  //   S
endmodule
