// Logisim project alu.circ as structural Verilog: 5 circuits, main circuit alu
module alu (
  input  [3:0] A,
  input  [3:0] B,
  input  [1:0] in_3,
  output [3:0] out_4
);

  wire [3:0] add_1_out_3, and_1_out_3, or_1_out_3, sub_1_out_3;

  add add_1 (.A(A), .B(B), .out_3(add_1_out_3));
  sub sub_1 (.A(A), .B(B), .out_3(sub_1_out_3));
  \and  and_1 (.A(A), .B(B), .out_3(and_1_out_3));
  \or  or_1 (.A(A), .B(B), .out_3(or_1_out_3));
  Multiplexer #(.select(2), .width(4)) multiplexer_1 (
    .in0(add_1_out_3), .in1(sub_1_out_3), .in2(and_1_out_3), .in3(or_1_out_3), .out(out_4), .sel(in_3));  // open: en
endmodule

module add (
  input  [3:0] A,
  input  [3:0] B,
  output [3:0] out_3
);

  Adder #(.width(4)) adder_1 (.a(A), .b(B), .out(out_3));  // open: cin, cout
endmodule

module sub (
  input  [3:0] A,
  input  [3:0] B,
  output [3:0] out_3
);

  Subtractor #(.width(4)) subtractor_1 (.a(A), .b(B), .out(out_3));  // open: bin, bout
endmodule

module \and  (
  input  [3:0] A,
  input  [3:0] B,
  output [3:0] out_3
);

  assign out_3 = A & B;  // AND_Gate and_1, 4 bits wide
endmodule

module \or  (
  input  [3:0] A,
  input  [3:0] B,
  output [3:0] out_3
);

  assign out_3 = A | B;  // OR_Gate or_1, 4 bits wide
endmodule
