// Logisim project fsm1.circ as structural Verilog: 1 circuit, main circuit fsm1
module fsm1 (
  input  in_1,
  input  [1:0] in_2,
  output out_3
);

  wire clock_1_out, not_1_out, not_2_out, not_3_out, register_1_q;
  wire [1:0] register_2_q, register_3_q;

  Clock clock_1 (.out(clock_1_out));
  Register #(.width(1)) register_1 (.D(in_1), .Q(register_1_q), .clk(clock_1_out), .clr(register_1_q));  // open: en
  Register #(.width(2)) register_2 (.D(in_2), .Q(register_2_q), .clk(clock_1_out), .clr(register_1_q));  // open: en
  Register #(.width(2)) register_3 (
    .D(register_2_q), .Q(register_3_q), .clk(clock_1_out), .clr(register_1_q));  // open: en
  not not_1 (not_1_out, register_3_q[1]);
  not not_2 (not_2_out, register_2_q[0]);
  not not_3 (not_3_out, in_2[0]);
  and and_1 (out_3, register_3_q[0], not_1_out, not_2_out, not_3_out);
endmodule
