// Logisim project grf.circ as structural Verilog: 1 circuit, main circuit grf
module grf (
  input  reset,
  input  WE,
  input  CLK,
  input  [4:0] A1,
  input  [4:0] A2,
  input  [4:0] A3,
  input  [31:0] in_7,
  output [31:0] RD1,
  output [31:0] RD2
);

  wire [31:0] r0, R1, r1_t, R2, r2_t, R3, r3_t, R4, r4_t, R5, r5_t, R6, r6_t, R7, r7_t, R8, r8_t, R9, r9_t,
       R10, r10_t, R11, r11_t, R12, r12_t, R13, r13_t, R14, r14_t, R15, r15_t, R16, r16_t, R17, r17_t, R18,
       r18_t, R19, r19_t, R20, r20_t, R21, r21_t, R22, r22_t, R23, r23_t, R24, r24_t, R25, r25_t, R26, r26_t,
       R27, r27_t, R28, r28_t, R29, r29_t, R30, r30_t, R31, r31_t;

  Demultiplexer #(.select(5), .width(32), .tristate("true")) demultiplexer_1 (
    .out1(R1), .out2(R2), .out3(R3), .out4(R4), .out5(R5), .out6(R6), .out7(R7), .out8(R8), .out9(R9),
    .out10(R10), .out11(R11), .out12(R12), .out13(R13), .out14(R14), .out15(R15), .out16(R16), .out17(R17),
    .out18(R18), .out19(R19), .out20(R20), .out21(R21), .out22(R22), .out23(R23), .out24(R24), .out25(R25),
    .out26(R26), .out27(R27), .out28(R28), .out29(R29), .out30(R30), .out31(R31), .in(in_7), .sel(A3), .en(WE));  // open: out0
  Register #(.width(32)) register_1 (.D({32{1'b0}}), .Q(r0), .clk(CLK), .clr(reset));  // open: en
  Register #(.width(32)) register_2 (.D(R1), .Q(r1_t), .clk(CLK), .clr(reset));  // open: en
  Register #(.width(32)) register_3 (.D(R2), .Q(r2_t), .clk(CLK), .clr(reset));  // open: en
  Register #(.width(32)) register_4 (.D(R3), .Q(r3_t), .clk(CLK), .clr(reset));  // open: en
  Register #(.width(32)) register_5 (.D(R4), .Q(r4_t), .clk(CLK), .clr(reset));  // open: en
  Register #(.width(32)) register_6 (.D(R5), .Q(r5_t), .clk(CLK), .clr(reset));  // open: en
  Register #(.width(32)) register_7 (.D(R6), .Q(r6_t), .clk(CLK), .clr(reset));  // open: en
  Register #(.width(32)) register_8 (.D(R7), .Q(r7_t), .clk(CLK), .clr(reset));  // open: en
  Register #(.width(32)) register_9 (.D(R8), .Q(r8_t), .clk(CLK), .clr(reset));  // open: en
  Register #(.width(32)) register_10 (.D(R9), .Q(r9_t), .clk(CLK), .clr(reset));  // open: en
  Register #(.width(32)) register_11 (.D(R10), .Q(r10_t), .clk(CLK), .clr(reset));  // open: en
  Register #(.width(32)) register_12 (.D(R11), .Q(r11_t), .clk(CLK), .clr(reset));  // open: en
  Register #(.width(32)) register_13 (.D(R12), .Q(r12_t), .clk(CLK), .clr(reset));  // open: en
  Register #(.width(32)) register_14 (.D(R13), .Q(r13_t), .clk(CLK), .clr(reset));  // open: en
  Register #(.width(32)) register_15 (.D(R14), .Q(r14_t), .clk(CLK), .clr(reset));  // open: en
  Register #(.width(32)) register_16 (.D(R15), .Q(r15_t), .clk(CLK), .clr(reset));  // open: en
  Register #(.width(32)) register_17 (.D(R16), .Q(r16_t), .clk(CLK), .clr(reset));  // open: en
  Register #(.width(32)) register_18 (.D(R17), .Q(r17_t), .clk(CLK), .clr(reset));  // open: en
  Register #(.width(32)) register_19 (.D(R18), .Q(r18_t), .clk(CLK), .clr(reset));  // open: en
  Register #(.width(32)) register_20 (.D(R19), .Q(r19_t), .clk(CLK), .clr(reset));  // open: en
  Register #(.width(32)) register_21 (.D(R20), .Q(r20_t), .clk(CLK), .clr(reset));  // open: en
  Register #(.width(32)) register_22 (.D(R21), .Q(r21_t), .clk(CLK), .clr(reset));  // open: en
  Register #(.width(32)) register_23 (.D(R22), .Q(r22_t), .clk(CLK), .clr(reset));  // open: en
  Register #(.width(32)) register_24 (.D(R23), .Q(r23_t), .clk(CLK), .clr(reset));  // open: en
  Register #(.width(32)) register_25 (.D(R24), .Q(r24_t), .clk(CLK), .clr(reset));  // open: en
  Register #(.width(32)) register_26 (.D(R25), .Q(r25_t), .clk(CLK), .clr(reset));  // open: en
  Register #(.width(32)) register_27 (.D(R26), .Q(r26_t), .clk(CLK), .clr(reset));  // open: en
  Register #(.width(32)) register_28 (.D(R27), .Q(r27_t), .clk(CLK), .clr(reset));  // open: en
  Register #(.width(32)) register_29 (.D(R28), .Q(r28_t), .clk(CLK), .clr(reset));  // open: en
  Register #(.width(32)) register_30 (.D(R29), .Q(r29_t), .clk(CLK), .clr(reset));  // open: en
  Register #(.width(32)) register_31 (.D(R30), .Q(r30_t), .clk(CLK), .clr(reset));  // open: en
  Register #(.width(32)) register_32 (.D(R31), .Q(r31_t), .clk(CLK), .clr(reset));  // open: en
  Multiplexer #(.select(5), .width(32)) multiplexer_1 (
    .in0(r0), .in1(r1_t), .in2(r2_t), .in3(r3_t), .in4(r4_t), .in5(r5_t), .in6(r6_t), .in7(r7_t), .in8(r8_t),
    .in9(r9_t), .in10(r10_t), .in11(r11_t), .in12(r12_t), .in13(r13_t), .in14(r14_t), .in15(r15_t),
    .in16(r16_t), .in17(r17_t), .in18(r18_t), .in19(r19_t), .in20(r20_t), .in21(r21_t), .in22(r22_t),
    .in23(r23_t), .in24(r24_t), .in25(r25_t), .in26(r26_t), .in27(r27_t), .in28(r28_t), .in29(r29_t),
    .in30(r30_t), .in31(r31_t), .out(RD1), .sel(A1));  // open: en
  Multiplexer #(.select(5), .width(32)) multiplexer_2 (
    .in0(r0), .in1(r1_t), .in2(r2_t), .in3(r3_t), .in4(r4_t), .in5(r5_t), .in6(r6_t), .in7(r7_t), .in8(r8_t),
    .in9(r9_t), .in10(r10_t), .in11(r11_t), .in12(r12_t), .in13(r13_t), .in14(r14_t), .in15(r15_t),
    .in16(r16_t), .in17(r17_t), .in18(r18_t), .in19(r19_t), .in20(r20_t), .in21(r21_t), .in22(r22_t),
    .in23(r23_t), .in24(r24_t), .in25(r25_t), .in26(r26_t), .in27(r27_t), .in28(r28_t), .in29(r29_t),
    .in30(r30_t), .in31(r31_t), .out(RD2), .sel(A2));  // open: en
endmodule
