// Logisim project grfyc.circ as structural Verilog: 2 circuits, main circuit grf
module grf (
  input  reset,
  input  WE,
  input  in_3,
  input  [4:0] A1,
  input  [4:0] A2,
  input  [4:0] A3,
  input  [31:0] in_7,
  output [31:0] out_8,
  output [31:0] out_9
);

  wire _0, _1, _2, _3, _4, _5, _6, _7, _8, _9, _10, _11, _12, _13, _14, _15, _16, _17, _18, _19, _20, _21,
       _22, _23, _24, _25, _26, _27, _28, _29, _30, _31, comparator_1_eq, comparator_2_eq, comparator_3_eq,
       comparator_4_eq, comparator_5_eq, comparator_6_eq, comparator_7_eq, comparator_8_eq, comparator_9_eq,
       comparator_10_eq, comparator_11_eq, comparator_12_eq, comparator_13_eq, comparator_14_eq,
       comparator_15_eq, comparator_16_eq, comparator_17_eq, comparator_18_eq, comparator_19_eq,
       comparator_20_eq, comparator_21_eq, comparator_22_eq, comparator_23_eq, comparator_24_eq,
       comparator_25_eq, comparator_26_eq, comparator_27_eq, comparator_28_eq, comparator_29_eq,
       comparator_30_eq, comparator_31_eq, comparator_32_eq;
  wire [31:0] _0_prime, _1_prime, _2_prime, _3_prime, _4_prime, _5_prime, _6_prime, _7_prime, _8_prime,
       _9_prime, _10_prime, _11_prime, _12_prime, _13_prime, _14_prime, _15_prime, _16_prime, _17_prime,
       _18_prime, _19_prime, _20_prime, _21_prime, _22_prime, _23_prime, _24_prime, _25_prime, _26_prime,
       _27_prime, _28_prime, _29_prime, _30_prime, _31_prime, multiplexer_2_out, multiplexer_3_out,
       multiplexer_4_out, multiplexer_5_out, multiplexer_6_out, multiplexer_7_out, multiplexer_8_out,
       multiplexer_9_out, multiplexer_10_out, multiplexer_11_out, multiplexer_12_out, multiplexer_13_out,
       multiplexer_14_out, multiplexer_15_out, multiplexer_16_out, multiplexer_17_out, multiplexer_18_out,
       multiplexer_19_out, multiplexer_20_out, multiplexer_21_out, multiplexer_22_out, multiplexer_23_out,
       multiplexer_24_out, multiplexer_25_out, multiplexer_26_out, multiplexer_27_out, multiplexer_28_out,
       multiplexer_29_out, multiplexer_30_out, multiplexer_31_out, multiplexer_32_out;

  Demultiplexer #(.select(5)) demultiplexer_1 (
    .out0(_0), .out1(_1), .out2(_2), .out3(_3), .out4(_4), .out5(_5), .out6(_6), .out7(_7), .out8(_8),
    .out9(_9), .out10(_10), .out11(_11), .out12(_12), .out13(_13), .out14(_14), .out15(_15), .out16(_16),
    .out17(_17), .out18(_18), .out19(_19), .out20(_20), .out21(_21), .out22(_22), .out23(_23), .out24(_24),
    .out25(_25), .out26(_26), .out27(_27), .out28(_28), .out29(_29), .out30(_30), .out31(_31), .in(1'b1),
    .sel(A3));  // open: en
  Comparator #(.width(1), .mode("unsigned")) comparator_1 (.a(_0), .b(1'b1), .eq(comparator_1_eq));  // open: gt, lt
  Comparator #(.width(1), .mode("unsigned")) comparator_2 (.a(_1), .b(1'b1), .eq(comparator_2_eq));  // open: gt, lt
  Comparator #(.width(1), .mode("unsigned")) comparator_3 (.a(_2), .b(1'b1), .eq(comparator_3_eq));  // open: gt, lt
  Comparator #(.width(1), .mode("unsigned")) comparator_4 (.a(_3), .b(1'b1), .eq(comparator_4_eq));  // open: gt, lt
  Comparator #(.width(1), .mode("unsigned")) comparator_5 (.a(_4), .b(1'b1), .eq(comparator_5_eq));  // open: gt, lt
  Comparator #(.width(1), .mode("unsigned")) comparator_6 (.a(_5), .b(1'b1), .eq(comparator_6_eq));  // open: gt, lt
  Comparator #(.width(1), .mode("unsigned")) comparator_7 (.a(_6), .b(1'b1), .eq(comparator_7_eq));  // open: gt, lt
  Comparator #(.width(1), .mode("unsigned")) comparator_8 (.a(_7), .b(1'b1), .eq(comparator_8_eq));  // open: gt, lt
  Comparator #(.width(1), .mode("unsigned")) comparator_9 (.a(_8), .b(1'b1), .eq(comparator_9_eq));  // open: gt, lt
  Comparator #(.width(1), .mode("unsigned")) comparator_10 (.a(_9), .b(1'b1), .eq(comparator_10_eq));  // open: gt, lt
  Comparator #(.width(1), .mode("unsigned")) comparator_11 (.a(_10), .b(1'b1), .eq(comparator_11_eq));  // open: gt, lt
  Comparator #(.width(1), .mode("unsigned")) comparator_12 (.a(_11), .b(1'b1), .eq(comparator_12_eq));  // open: gt, lt
  Comparator #(.width(1), .mode("unsigned")) comparator_13 (.a(_12), .b(1'b1), .eq(comparator_13_eq));  // open: gt, lt
  Comparator #(.width(1), .mode("unsigned")) comparator_14 (.a(_13), .b(1'b1), .eq(comparator_14_eq));  // open: gt, lt
  Comparator #(.width(1), .mode("unsigned")) comparator_15 (.a(_14), .b(1'b1), .eq(comparator_15_eq));  // open: gt, lt
  Comparator #(.width(1), .mode("unsigned")) comparator_16 (.a(_15), .b(1'b1), .eq(comparator_16_eq));  // open: gt, lt
  Comparator #(.width(1), .mode("unsigned")) comparator_17 (.a(_16), .b(1'b1), .eq(comparator_17_eq));  // open: gt, lt
  Comparator #(.width(1), .mode("unsigned")) comparator_18 (.a(_17), .b(1'b1), .eq(comparator_18_eq));  // open: gt, lt
  Comparator #(.width(1), .mode("unsigned")) comparator_19 (.a(_18), .b(1'b1), .eq(comparator_19_eq));  // open: gt, lt
  Comparator #(.width(1), .mode("unsigned")) comparator_20 (.a(_19), .b(1'b1), .eq(comparator_20_eq));  // open: gt, lt
  Comparator #(.width(1), .mode("unsigned")) comparator_21 (.a(_20), .b(1'b1), .eq(comparator_21_eq));  // open: gt, lt
  Comparator #(.width(1), .mode("unsigned")) comparator_22 (.a(_21), .b(1'b1), .eq(comparator_22_eq));  // open: gt, lt
  Comparator #(.width(1), .mode("unsigned")) comparator_23 (.a(_22), .b(1'b1), .eq(comparator_23_eq));  // open: gt, lt
  Comparator #(.width(1), .mode("unsigned")) comparator_24 (.a(_23), .b(1'b1), .eq(comparator_24_eq));  // open: gt, lt
  Comparator #(.width(1), .mode("unsigned")) comparator_25 (.a(_24), .b(1'b1), .eq(comparator_25_eq));  // open: gt, lt
  Comparator #(.width(1), .mode("unsigned")) comparator_26 (.a(_25), .b(1'b1), .eq(comparator_26_eq));  // open: gt, lt
  Comparator #(.width(1), .mode("unsigned")) comparator_27 (.a(_26), .b(1'b1), .eq(comparator_27_eq));  // open: gt, lt
  Comparator #(.width(1), .mode("unsigned")) comparator_28 (.a(_27), .b(1'b1), .eq(comparator_28_eq));  // open: gt, lt
  Comparator #(.width(1), .mode("unsigned")) comparator_29 (.a(_28), .b(1'b1), .eq(comparator_29_eq));  // open: gt, lt
  Comparator #(.width(1), .mode("unsigned")) comparator_30 (.a(_29), .b(1'b1), .eq(comparator_30_eq));  // open: gt, lt
  Comparator #(.width(1), .mode("unsigned")) comparator_31 (.a(_30), .b(1'b1), .eq(comparator_31_eq));  // open: gt, lt
  Comparator #(.width(1), .mode("unsigned")) comparator_32 (.a(_31), .b(1'b1), .eq(comparator_32_eq));  // open: gt, lt
  Multiplexer #(.width(32)) multiplexer_1 (
    .in0({32{1'b0}}), .in1({32{1'b0}}), .out(_0_prime), .sel(comparator_1_eq));  // open: en
  Multiplexer #(.width(32)) multiplexer_2 (
    .in0(_1_prime), .in1(in_7), .out(multiplexer_2_out), .sel(comparator_2_eq));  // open: en
  Multiplexer #(.width(32)) multiplexer_3 (
    .in0(_2_prime), .in1(in_7), .out(multiplexer_3_out), .sel(comparator_3_eq));  // open: en
  Multiplexer #(.width(32)) multiplexer_4 (
    .in0(_3_prime), .in1(in_7), .out(multiplexer_4_out), .sel(comparator_4_eq));  // open: en
  Multiplexer #(.width(32)) multiplexer_5 (
    .in0(_4_prime), .in1(in_7), .out(multiplexer_5_out), .sel(comparator_5_eq));  // open: en
  Multiplexer #(.width(32)) multiplexer_6 (
    .in0(_5_prime), .in1(in_7), .out(multiplexer_6_out), .sel(comparator_6_eq));  // open: en
  Multiplexer #(.width(32)) multiplexer_7 (
    .in0(_6_prime), .in1(in_7), .out(multiplexer_7_out), .sel(comparator_7_eq));  // open: en
  Multiplexer #(.width(32)) multiplexer_8 (
    .in0(_7_prime), .in1(in_7), .out(multiplexer_8_out), .sel(comparator_8_eq));  // open: en
  Multiplexer #(.width(32)) multiplexer_9 (
    .in0(_8_prime), .in1(in_7), .out(multiplexer_9_out), .sel(comparator_9_eq));  // open: en
  Multiplexer #(.width(32)) multiplexer_10 (
    .in0(_9_prime), .in1(in_7), .out(multiplexer_10_out), .sel(comparator_10_eq));  // open: en
  Multiplexer #(.width(32)) multiplexer_11 (
    .in0(_10_prime), .in1(in_7), .out(multiplexer_11_out), .sel(comparator_11_eq));  // open: en
  Multiplexer #(.width(32)) multiplexer_12 (
    .in0(_11_prime), .in1(in_7), .out(multiplexer_12_out), .sel(comparator_12_eq));  // open: en
  Multiplexer #(.width(32)) multiplexer_13 (
    .in0(_12_prime), .in1(in_7), .out(multiplexer_13_out), .sel(comparator_13_eq));  // open: en
  Multiplexer #(.width(32)) multiplexer_14 (
    .in0(_13_prime), .in1(in_7), .out(multiplexer_14_out), .sel(comparator_14_eq));  // open: en
  Multiplexer #(.width(32)) multiplexer_15 (
    .in0(_14_prime), .in1(in_7), .out(multiplexer_15_out), .sel(comparator_15_eq));  // open: en
  Multiplexer #(.width(32)) multiplexer_16 (
    .in0(_15_prime), .in1(in_7), .out(multiplexer_16_out), .sel(comparator_16_eq));  // open: en
  Multiplexer #(.width(32)) multiplexer_17 (
    .in0(_16_prime), .in1(in_7), .out(multiplexer_17_out), .sel(comparator_17_eq));  // open: en
  Multiplexer #(.width(32)) multiplexer_18 (
    .in0(_17_prime), .in1(in_7), .out(multiplexer_18_out), .sel(comparator_18_eq));  // open: en
  Multiplexer #(.width(32)) multiplexer_19 (
    .in0(_18_prime), .in1(in_7), .out(multiplexer_19_out), .sel(comparator_19_eq));  // open: en
  Multiplexer #(.width(32)) multiplexer_20 (
    .in0(_19_prime), .in1(in_7), .out(multiplexer_20_out), .sel(comparator_20_eq));  // open: en
  Multiplexer #(.width(32)) multiplexer_21 (
    .in0(_20_prime), .in1(in_7), .out(multiplexer_21_out), .sel(comparator_21_eq));  // open: en
  Multiplexer #(.width(32)) multiplexer_22 (
    .in0(_21_prime), .in1(in_7), .out(multiplexer_22_out), .sel(comparator_22_eq));  // open: en
  Multiplexer #(.width(32)) multiplexer_23 (
    .in0(_22_prime), .in1(in_7), .out(multiplexer_23_out), .sel(comparator_23_eq));  // open: en
  Multiplexer #(.width(32)) multiplexer_24 (
    .in0(_23_prime), .in1(in_7), .out(multiplexer_24_out), .sel(comparator_24_eq));  // open: en
  Multiplexer #(.width(32)) multiplexer_25 (
    .in0(_24_prime), .in1(in_7), .out(multiplexer_25_out), .sel(comparator_25_eq));  // open: en
  Multiplexer #(.width(32)) multiplexer_26 (
    .in0(_25_prime), .in1(in_7), .out(multiplexer_26_out), .sel(comparator_26_eq));  // open: en
  Multiplexer #(.width(32)) multiplexer_27 (
    .in0(_26_prime), .in1(in_7), .out(multiplexer_27_out), .sel(comparator_27_eq));  // open: en
  Multiplexer #(.width(32)) multiplexer_28 (
    .in0(_27_prime), .in1(in_7), .out(multiplexer_28_out), .sel(comparator_28_eq));  // open: en
  Multiplexer #(.width(32)) multiplexer_29 (
    .in0(_28_prime), .in1(in_7), .out(multiplexer_29_out), .sel(comparator_29_eq));  // open: en
  Multiplexer #(.width(32)) multiplexer_30 (
    .in0(_29_prime), .in1(in_7), .out(multiplexer_30_out), .sel(comparator_30_eq));  // open: en
  Multiplexer #(.width(32)) multiplexer_31 (
    .in0(_30_prime), .in1(in_7), .out(multiplexer_31_out), .sel(comparator_31_eq));  // open: en
  Multiplexer #(.width(32)) multiplexer_32 (
    .in0(_31_prime), .in1(in_7), .out(multiplexer_32_out), .sel(comparator_32_eq));  // open: en
  _1_register u_1_register_1 (.in_4(multiplexer_2_out), .in_1(reset), .reset(WE), .WE(in_3), .out_5(_1_prime));
  _1_register u_1_register_2 (.in_4(multiplexer_3_out), .in_1(reset), .reset(WE), .WE(in_3), .out_5(_2_prime));
  _1_register u_1_register_3 (.in_4(multiplexer_4_out), .in_1(reset), .reset(WE), .WE(in_3), .out_5(_3_prime));
  _1_register u_1_register_4 (.in_4(multiplexer_5_out), .in_1(reset), .reset(WE), .WE(in_3), .out_5(_4_prime));
  _1_register u_1_register_5 (.in_4(multiplexer_6_out), .in_1(reset), .reset(WE), .WE(in_3), .out_5(_5_prime));
  _1_register u_1_register_6 (.in_4(multiplexer_7_out), .in_1(reset), .reset(WE), .WE(in_3), .out_5(_6_prime));
  _1_register u_1_register_7 (.in_4(multiplexer_8_out), .in_1(reset), .reset(WE), .WE(in_3), .out_5(_7_prime));
  _1_register u_1_register_8 (.in_4(multiplexer_9_out), .in_1(reset), .reset(WE), .WE(in_3), .out_5(_8_prime));
  _1_register u_1_register_9 (.in_4(multiplexer_10_out), .in_1(reset), .reset(WE), .WE(in_3), .out_5(_9_prime));
  _1_register u_1_register_10 (.in_4(multiplexer_11_out), .in_1(reset), .reset(WE), .WE(in_3), .out_5(_10_prime));
  _1_register u_1_register_11 (.in_4(multiplexer_12_out), .in_1(reset), .reset(WE), .WE(in_3), .out_5(_11_prime));
  _1_register u_1_register_12 (.in_4(multiplexer_13_out), .in_1(reset), .reset(WE), .WE(in_3), .out_5(_12_prime));
  _1_register u_1_register_13 (.in_4(multiplexer_14_out), .in_1(reset), .reset(WE), .WE(in_3), .out_5(_13_prime));
  _1_register u_1_register_14 (.in_4(multiplexer_15_out), .in_1(reset), .reset(WE), .WE(in_3), .out_5(_14_prime));
  _1_register u_1_register_15 (.in_4(multiplexer_16_out), .in_1(reset), .reset(WE), .WE(in_3), .out_5(_15_prime));
  _1_register u_1_register_16 (.in_4(multiplexer_17_out), .in_1(reset), .reset(WE), .WE(in_3), .out_5(_16_prime));
  _1_register u_1_register_17 (.in_4(multiplexer_18_out), .in_1(reset), .reset(WE), .WE(in_3), .out_5(_17_prime));
  _1_register u_1_register_18 (.in_4(multiplexer_19_out), .in_1(reset), .reset(WE), .WE(in_3), .out_5(_18_prime));
  _1_register u_1_register_19 (.in_4(multiplexer_20_out), .in_1(reset), .reset(WE), .WE(in_3), .out_5(_19_prime));
  _1_register u_1_register_20 (.in_4(multiplexer_21_out), .in_1(reset), .reset(WE), .WE(in_3), .out_5(_20_prime));
  _1_register u_1_register_21 (.in_4(multiplexer_22_out), .in_1(reset), .reset(WE), .WE(in_3), .out_5(_21_prime));
  _1_register u_1_register_22 (.in_4(multiplexer_23_out), .in_1(reset), .reset(WE), .WE(in_3), .out_5(_22_prime));
  _1_register u_1_register_23 (.in_4(multiplexer_24_out), .in_1(reset), .reset(WE), .WE(in_3), .out_5(_23_prime));
  _1_register u_1_register_24 (.in_4(multiplexer_25_out), .in_1(reset), .reset(WE), .WE(in_3), .out_5(_24_prime));
  _1_register u_1_register_25 (.in_4(multiplexer_26_out), .in_1(reset), .reset(WE), .WE(in_3), .out_5(_25_prime));
  _1_register u_1_register_26 (.in_4(multiplexer_27_out), .in_1(reset), .reset(WE), .WE(in_3), .out_5(_26_prime));
  _1_register u_1_register_27 (.in_4(multiplexer_28_out), .in_1(reset), .reset(WE), .WE(in_3), .out_5(_27_prime));
  _1_register u_1_register_28 (.in_4(multiplexer_29_out), .in_1(reset), .reset(WE), .WE(in_3), .out_5(_28_prime));
  _1_register u_1_register_29 (.in_4(multiplexer_30_out), .in_1(reset), .reset(WE), .WE(in_3), .out_5(_29_prime));
  _1_register u_1_register_30 (.in_4(multiplexer_31_out), .in_1(reset), .reset(WE), .WE(in_3), .out_5(_30_prime));
  _1_register u_1_register_31 (.in_4(multiplexer_32_out), .in_1(reset), .reset(WE), .WE(in_3), .out_5(_31_prime));
  Multiplexer #(.select(5), .width(32)) multiplexer_33 (
    .in0(_0_prime), .in1(_1_prime), .in2(_2_prime), .in3(_3_prime), .in4(_4_prime), .in5(_5_prime),
    .in6(_6_prime), .in7(_7_prime), .in8(_8_prime), .in9(_9_prime), .in10(_10_prime), .in11(_11_prime),
    .in12(_12_prime), .in13(_13_prime), .in14(_14_prime), .in15(_15_prime), .in16(_16_prime),
    .in17(_17_prime), .in18(_18_prime), .in19(_19_prime), .in20(_20_prime), .in21(_21_prime),
    .in22(_22_prime), .in23(_23_prime), .in24(_24_prime), .in25(_25_prime), .in26(_26_prime),
    .in27(_27_prime), .in28(_28_prime), .in29(_29_prime), .in30(_30_prime), .in31(_31_prime), .out(out_8),
    .sel(A1));  // open: en
  Multiplexer #(.select(5), .width(32)) multiplexer_34 (
    .in0(_0_prime), .in1(_1_prime), .in2(_2_prime), .in3(_3_prime), .in4(_4_prime), .in5(_5_prime),
    .in6(_6_prime), .in7(_7_prime), .in8(_8_prime), .in9(_9_prime), .in10(_10_prime), .in11(_11_prime),
    .in12(_12_prime), .in13(_13_prime), .in14(_14_prime), .in15(_15_prime), .in16(_16_prime),
    .in17(_17_prime), .in18(_18_prime), .in19(_19_prime), .in20(_20_prime), .in21(_21_prime),
    .in22(_22_prime), .in23(_23_prime), .in24(_24_prime), .in25(_25_prime), .in26(_26_prime),
    .in27(_27_prime), .in28(_28_prime), .in29(_29_prime), .in30(_30_prime), .in31(_31_prime), .out(out_9),
    .sel(A2));  // open: en

  // Other names for the same wires on the sheet: CLK = reset
endmodule

module _1_register (
  input  in_1,
  input  reset,
  input  WE,
  input  [31:0] in_4,
  output [31:0] out_5
);

  wire [31:0] multiplexer_1_out;

  Multiplexer #(.select(2), .width(32)) multiplexer_1 (
    .in0(out_5), .in1(in_4), .in2({32{1'b0}}), .in3({32{1'b0}}), .out(multiplexer_1_out), .sel({reset, WE}));  // open: en
  Register #(.width(32)) register_1 (.D(multiplexer_1_out), .Q(out_5), .clk(in_1));  // open: en, clr
endmodule
