// Logisim project mod5.circ as structural Verilog: 1 circuit, main circuit mod5
module mod5 (
  input  in_1,
  output out_2,
  output out_3,
  output out_4,
  output out_5,
  output out_6
);

  wire and_2_out, and_3_out, and_4_out, and_5_out, and_6_out, and_7_out, and_8_out, and_9_out, and_10_out,
       and_11_out, and_12_out, and_13_out, and_14_out, and_15_out, clock_1_out, not_1_out, not_2_out,
       not_3_out, or_1_out, or_2_out, register_1_q, register_2_q;

  not not_1 (not_1_out, register_1_q);
  not not_2 (not_2_out, in_1);
  not not_3 (not_3_out, register_2_q);
  and and_1 (out_2, register_2_q, register_2_q, not_3_out);
  and and_2 (and_2_out, not_1_out, register_2_q, not_2_out);
  and and_3 (and_3_out, not_1_out, not_3_out, in_1);
  and and_4 (and_4_out, register_1_q, not_3_out, not_2_out);
  and and_5 (and_5_out, in_1, register_1_q, register_2_q);
  and and_6 (and_6_out, register_2_q, not_1_out);
  and and_7 (and_7_out, not_3_out, register_1_q);
  and and_8 (and_8_out, not_2_out, not_1_out, not_1_out, not_3_out);
  and and_9 (and_9_out, not_2_out, register_1_q, register_2_q);
  and and_10 (and_10_out, not_3_out, not_1_out, in_1);
  and and_11 (and_11_out, in_1, register_1_q, register_2_q);
  or or_1 (or_1_out, and_2_out, and_3_out, and_4_out, and_5_out);
  or or_2 (or_2_out, and_6_out, and_7_out);
  or or_3 (out_3, and_8_out, and_9_out);
  or or_4 (out_4, and_10_out, and_11_out);
  Clock clock_1 (.out(clock_1_out));
  or or_5 (out_5, and_12_out, and_13_out);
  and and_12 (and_12_out, register_2_q, not_1_out, in_1);
  Register #(.width(1)) register_1 (.D(or_2_out), .Q(register_1_q), .clk(clock_1_out));  // open: en, clr
  Register #(.width(1)) register_2 (.D(or_1_out), .Q(register_2_q), .clk(clock_1_out));  // open: en, clr
  and and_13 (and_13_out, not_3_out, register_1_q, in_1);
  and and_14 (and_14_out, not_3_out, register_1_q, not_2_out);
  or or_6 (out_6, and_14_out, and_15_out);
  and and_15 (and_15_out, register_2_q, not_1_out, not_2_out);

  // Notes on the sheet:
  //   s1'
  //   s0'
  //   s1
  //   s0
endmodule
