// Logisim project sortswap.circ as structural Verilog: 3 circuits, main circuit 4bit_sort
module _4bit_sort (
  input  [3:0] data1,
  input  [3:0] data2,
  input  [3:0] data3,
  input  [3:0] data4,
  output [3:0] out_5,
  output [3:0] out_6,
  output [3:0] out_7,
  output [3:0] out_8
);

  wire comparator_1_gt, comparator_2_gt, comparator_3_gt, comparator_4_gt, comparator_5_gt, comparator_6_gt;
  wire [3:0] n4bit_swap_1_out_4, n4bit_swap_1_out_5, n4bit_swap_2_out_4, n4bit_swap_2_out_5,
       n4bit_swap_3_out_4, n4bit_swap_3_out_5, n4bit_swap_4_out_5, n4bit_swap_6_out_5;

  Comparator #(.width(4), .mode("unsigned")) comparator_1 (.a(data1), .b(data2), .gt(comparator_1_gt));  // open: eq, lt
  Comparator #(.width(4), .mode("unsigned")) comparator_2 (
    .a(n4bit_swap_1_out_5), .b(n4bit_swap_3_out_5), .gt(comparator_2_gt));  // open: eq, lt
  _4bit_swap u_4bit_swap_1 (
    .data1(data1), .data2(data2), .judge(comparator_1_gt), .out_4(n4bit_swap_1_out_4),
    .out_5(n4bit_swap_1_out_5));
  _4bit_swap u_4bit_swap_2 (
    .data1(n4bit_swap_1_out_5), .data2(n4bit_swap_3_out_5), .judge(comparator_2_gt),
    .out_4(n4bit_swap_2_out_4), .out_5(n4bit_swap_2_out_5));
  Comparator #(.width(4), .mode("unsigned")) comparator_3 (
    .a(n4bit_swap_1_out_4), .b(data3), .gt(comparator_3_gt));  // open: eq, lt
  Comparator #(.width(4), .mode("unsigned")) comparator_4 (
    .a(n4bit_swap_2_out_4), .b(n4bit_swap_6_out_5), .gt(comparator_4_gt));  // open: eq, lt
  Comparator #(.width(4), .mode("unsigned")) comparator_5 (
    .a(n4bit_swap_2_out_5), .b(n4bit_swap_4_out_5), .gt(comparator_5_gt));  // open: eq, lt
  _4bit_swap u_4bit_swap_3 (
    .data1(n4bit_swap_1_out_4), .data2(data3), .judge(comparator_3_gt), .out_4(n4bit_swap_3_out_4),
    .out_5(n4bit_swap_3_out_5));
  Comparator #(.width(4), .mode("unsigned")) comparator_6 (
    .a(n4bit_swap_3_out_4), .b(data4), .gt(comparator_6_gt));  // open: eq, lt
  _4bit_swap u_4bit_swap_4 (
    .data1(n4bit_swap_2_out_4), .data2(n4bit_swap_6_out_5), .judge(comparator_4_gt), .out_4(out_6),
    .out_5(n4bit_swap_4_out_5));
  _4bit_swap u_4bit_swap_5 (
    .data1(n4bit_swap_2_out_5), .data2(n4bit_swap_4_out_5), .judge(comparator_5_gt), .out_4(out_7),
    .out_5(out_8));
  _4bit_swap u_4bit_swap_6 (
    .data1(n4bit_swap_3_out_4), .data2(data4), .judge(comparator_6_gt), .out_4(out_5),
    .out_5(n4bit_swap_6_out_5));
endmodule

module _1bit_swap (
  input  l1,
  input  l2,
  input  s,
  output O1,
  output O2
);

  wire and_1_out, and_2_out, and_3_out, and_4_out, not_1_out, not_2_out;

  not not_1 (not_1_out, s);
  not not_2 (not_2_out, s);
  and and_1 (and_1_out, l2, s);
  and and_2 (and_2_out, l1, not_1_out);
  and and_3 (and_3_out, l2, not_2_out);
  and and_4 (and_4_out, l1, s);
  or or_1 (O1, and_1_out, and_2_out);
  or or_2 (O2, and_3_out, and_4_out);
endmodule

module _4bit_swap (
  input  [3:0] data1,
  input  [3:0] data2,
  input  judge,
  output [3:0] out_4,
  output [3:0] out_5
);

  _1bit_swap u_1bit_swap_1 (.l1(data1[0]), .l2(data2[0]), .s(judge), .O1(out_4[0]), .O2(out_5[0]));
  _1bit_swap u_1bit_swap_2 (.l1(data1[1]), .l2(data2[1]), .s(judge), .O1(out_4[1]), .O2(out_5[1]));
  _1bit_swap u_1bit_swap_3 (.l1(data1[2]), .l2(data2[2]), .s(judge), .O1(out_4[2]), .O2(out_5[2]));
  _1bit_swap u_1bit_swap_4 (.l1(data1[3]), .l2(data2[3]), .s(judge), .O1(out_4[3]), .O2(out_5[3]));
endmodule
