// Logisim project 全加器.circ as structural Verilog: 1 circuit, main circuit main
module main (
  input  [1:0] A,
  input  [1:0] B,
  input  CI,
  output [1:0] SUM,
  output CO
);

  wire and_1_out, and_2_out, and_3_out, and_4_out, and_5_out, and_6_out, and_7_out, and_8_out, and_9_out,
       and_10_out, and_11_out, and_12_out, and_13_out, and_14_out, and_15_out, and_16_out, and_17_out,
       and_18_out, not_1_out, not_2_out, not_3_out, not_4_out, not_5_out, not_6_out, not_7_out, not_8_out,
       not_9_out, not_10_out, not_11_out, not_12_out, not_13_out, not_14_out, not_15_out, not_16_out,
       not_17_out, not_18_out, not_19_out, not_20_out, not_21_out, not_22_out, not_23_out, not_24_out,
       not_25_out, not_26_out, not_27_out, not_28_out, not_29_out, not_30_out, not_31_out, not_32_out,
       not_33_out, not_34_out, not_35_out, not_36_out, not_37_out, not_38_out, not_39_out, not_40_out,
       not_41_out, not_42_out, not_43_out, not_44_out, not_45_out, not_46_out, not_47_out;

  not not_1 (not_1_out, A[1]);
  not not_2 (not_2_out, A[0]);
  not not_3 (not_3_out, A[1]);
  not not_4 (not_4_out, A[0]);
  not not_5 (not_5_out, CI);
  not not_6 (not_6_out, A[1]);
  not not_7 (not_7_out, B[1]);
  not not_8 (not_8_out, B[0]);
  not not_9 (not_9_out, A[1]);
  not not_10 (not_10_out, B[1]);
  not not_11 (not_11_out, CI);
  not not_12 (not_12_out, A[0]);
  not not_13 (not_13_out, B[1]);
  not not_14 (not_14_out, B[0]);
  not not_15 (not_15_out, CI);
  not not_16 (not_16_out, A[0]);
  not not_17 (not_17_out, B[0]);
  not not_18 (not_18_out, A[1]);
  not not_19 (not_19_out, A[0]);
  not not_20 (not_20_out, B[1]);
  not not_21 (not_21_out, B[0]);
  not not_22 (not_22_out, A[1]);
  not not_23 (not_23_out, A[0]);
  not not_24 (not_24_out, CI);
  not not_25 (not_25_out, A[1]);
  not not_26 (not_26_out, B[1]);
  not not_27 (not_27_out, B[0]);
  not not_28 (not_28_out, CI);
  not not_29 (not_29_out, A[1]);
  not not_30 (not_30_out, B[0]);
  not not_31 (not_31_out, A[0]);
  not not_32 (not_32_out, B[1]);
  not not_33 (not_33_out, A[0]);
  not not_34 (not_34_out, B[0]);
  not not_35 (not_35_out, CI);
  not not_36 (not_36_out, A[0]);
  not not_37 (not_37_out, B[0]);
  not not_38 (not_38_out, A[1]);
  not not_39 (not_39_out, B[1]);
  not not_40 (not_40_out, A[1]);
  not not_41 (not_41_out, B[0]);
  not not_42 (not_42_out, A[0]);
  not not_43 (not_43_out, B[1]);
  not not_44 (not_44_out, A[0]);
  not not_45 (not_45_out, B[1]);
  not not_46 (not_46_out, A[0]);
  not not_47 (not_47_out, B[0]);
  and and_1 (and_1_out, not_1_out, not_2_out, B[0], CI);
  and and_2 (and_2_out, not_3_out, not_4_out, B[1], not_5_out);
  and and_3 (and_3_out, not_6_out, A[0], not_7_out, not_8_out, CI);
  and and_4 (and_4_out, not_9_out, A[0], not_10_out, B[0], not_11_out);
  and and_5 (and_5_out, A[1], not_12_out, not_13_out, not_14_out, not_15_out);
  and and_6 (and_6_out, A[1], not_16_out, B[1], not_17_out, CI);
  and and_7 (and_7_out, not_18_out, not_19_out, not_20_out, not_21_out, CI);
  and and_8 (and_8_out, not_22_out, not_23_out, B[0], not_24_out);
  and and_9 (and_9_out, not_25_out, A[0], not_26_out, not_27_out, not_28_out);
  and and_10 (and_10_out, not_29_out, A[0], B[1], not_30_out, CI);
  and and_11 (and_11_out, A[1], not_31_out, not_32_out, B[0], CI);
  and and_12 (and_12_out, A[1], not_33_out, B[1], not_34_out, not_35_out);
  and and_13 (and_13_out, not_36_out, B[1], not_37_out, CI);
  and and_14 (and_14_out, not_38_out, A[0], not_39_out, B[0], CI);
  and and_15 (and_15_out, not_40_out, A[0], B[1], not_41_out);
  and and_16 (and_16_out, A[1], not_42_out, not_43_out, CI);
  and and_17 (and_17_out, A[1], not_44_out, not_45_out, B[0]);
  and and_18 (and_18_out, A[1], not_46_out, B[1], not_47_out);
  or or_1 (SUM[1], and_1_out, and_2_out, and_3_out, and_4_out, and_5_out, and_6_out);
  or or_2 (SUM[0], and_7_out, and_8_out, and_9_out, and_10_out, and_11_out, and_12_out);
  or or_3 (CO, and_13_out, and_14_out, and_15_out, and_16_out, and_17_out, and_18_out);
endmodule
