// Logisim project 半加器.circ as structural Verilog: 1 circuit, main circuit main
module main (
  input  [1:0] A,
  input  [1:0] B,
  output [1:0] sum,
  output carry
);

  wire and_1_out, and_2_out, and_3_out, and_4_out, and_5_out, and_6_out, and_7_out, and_8_out, and_9_out,
       not_1_out, not_2_out, not_3_out, not_4_out;

  not not_1 (not_1_out, A[0]);
  not not_2 (not_2_out, A[1]);
  not not_3 (not_3_out, B[0]);
  not not_4 (not_4_out, B[1]);
  and and_1 (and_1_out, not_1_out, not_2_out, B[0], not_4_out);
  and and_2 (and_2_out, A[0], not_2_out, not_3_out, not_4_out);
  and and_3 (and_3_out, not_1_out, A[1], not_3_out, B[1]);
  and and_4 (and_4_out, not_1_out, not_2_out, not_3_out, B[1]);
  and and_5 (and_5_out, A[0], not_2_out, B[0], not_4_out);
  and and_6 (and_6_out, not_1_out, A[1], not_3_out, not_4_out);
  and and_7 (and_7_out, not_1_out, A[1], not_3_out, B[1]);
  and and_8 (and_8_out, A[0], not_2_out, not_3_out, B[1]);
  and and_9 (and_9_out, not_1_out, A[1], B[0], not_4_out);
  or or_1 (sum[0], and_1_out, and_2_out, and_3_out);
  or or_2 (sum[1], and_4_out, and_5_out, and_6_out);
  or or_3 (carry, and_7_out, and_8_out, and_9_out);

  // Notes on the sheet:
  //   A0
  //   A1
  //   B0
  //   B1
endmodule
