// Logisim project 斐波那契.circ as structural Verilog: 1 circuit, main circuit main
module main (
  input  [2:0] in_1,
  output [3:0] out_2
);

  wire clock_1_out, comparator_2_gt, comparator_3_eq, register_1_q, register_3_q, register_4_q, register_5_q;
  wire [1:0] comparator_1_gt;
  wire [3:0] adder_1_out, counter_1_q, counter_2_q, counter_3_q, multiplexer_1_out, multiplexer_2_out,
       register_2_q, register_6_q;

  Clock clock_1 (.out(clock_1_out));
  Counter #(.width(4), .max('hf), .ongoal("stay")) counter_1 (
    .Q(counter_1_q), .clk(clock_1_out));  // open: load, D, count, carry, clr
  Counter #(.width(4), .max('hf), .ongoal("stay")) counter_2 (
    .Q(counter_2_q), .clk(clock_1_out));  // open: load, D, count, carry, clr
  Counter #(.width(4), .max('hf), .ongoal("stay")) counter_3 (
    .Q(counter_3_q), .clk(clock_1_out));  // open: load, D, count, carry, clr
  Comparator #(.width(4), .mode("unsigned")) comparator_1 (
    .a(counter_1_q), .b(4'b0010), .gt(comparator_1_gt[0]), .eq(comparator_1_gt[1]));  // open: lt
  Comparator #(.width(4), .mode("unsigned")) comparator_2 (
    .a(counter_2_q), .b(4'b0001), .gt(comparator_2_gt));  // open: eq, lt
  Comparator #(.width(4), .mode("unsigned")) comparator_3 (
    .a({1'b0, in_1}), .b(counter_3_q), .eq(comparator_3_eq));  // open: gt, lt
  Register #(.width(1)) register_1 (.D(comparator_3_eq), .Q(register_1_q), .clk(clock_1_out));  // open: en, clr
  Register #(.width(4)) register_2 (.D(multiplexer_1_out), .Q(register_2_q), .clk(clock_1_out));  // open: en, clr
  Multiplexer #(.select(2), .width(4)) multiplexer_1 (
    .in0(4'b0000), .in1(register_6_q), .in2(4'b0001), .out(multiplexer_1_out), .sel(comparator_1_gt));  // open: in3, en
  Multiplexer #(.width(4)) multiplexer_2 (
    .in0(4'b0000), .in1(register_6_q), .out(multiplexer_2_out), .sel(comparator_2_gt));  // open: en
  Register #(.width(1)) register_3 (.D(register_4_q), .Q(register_3_q), .clk(clock_1_out));  // open: en, clr
  Register #(.width(1)) register_4 (.D(register_1_q), .Q(register_4_q), .clk(clock_1_out));  // open: en, clr
  Adder #(.width(4)) adder_1 (.a(register_2_q), .b(multiplexer_2_out), .out(adder_1_out));  // open: cin, cout
  Register #(.width(1)) register_5 (.D(register_3_q), .Q(register_5_q), .clk(clock_1_out));  // open: en, clr
  Register #(.width(4)) register_6 (.D(adder_1_out), .Q(register_6_q), .clk(clock_1_out));  // open: en, clr
  Register #(.width(4)) register_7 (.D(register_2_q), .en(register_5_q), .Q(out_2), .clk(clock_1_out));  // open: clr

  // Notes on the sheet:
  //   与2作比较
  //   与1作比较
  //   输入的数字与第几次变化作比较，由此作为使能端
endmodule
