// Logisim project 斐波那契challenge.circ as structural Verilog: 3 circuits, main circuit main
module main (
  input  [31:0] in_1,
  output [31:0] out_2
);

  wire clock_1_out, comparator_1_gt, comparator_2_gt, comparator_3_eq, comparator_4_eq, multiplexer_1_out,
       register_1_q, register_2_q;
  wire [4:0] counter_2_q;
  wire [7:0] counter_1_q, counter_3_q;
  wire [31:0] ans_1_out_10, ans_1_out_11, ans_1_out_12, ans_1_out_13, counter_4_q, multiplexer_2_out,
       multiplexer_3_out, multiplexer_4_out, multiplexer_5_out, multiplexer_6_out, multiplexer_7_out,
       multiplexer_8_out, multiplexer_9_out, register_4_q, register_5_q, register_6_q, register_7_q,
       register_8_q, register_9_q, register_10_q, register_11_q, res_1_out_5, res_1_out_6, res_1_out_7,
       res_1_out_8;

  Clock clock_1 (.out(clock_1_out));
  Counter #(.ongoal("stay")) counter_1 (.Q(counter_1_q), .clk(clock_1_out));  // open: load, D, count, carry, clr
  Counter #(.width(5), .max('h1f), .ongoal("stay")) counter_2 (
    .Q(counter_2_q), .clk(clock_1_out));  // open: load, D, count, carry, clr
  Counter #(.ongoal("stay")) counter_3 (.Q(counter_3_q), .clk(clock_1_out));  // open: load, D, count, carry, clr
  Counter #(.width(32), .max('hffffffff), .ongoal("stay")) counter_4 (
    .Q(counter_4_q), .clk(clock_1_out));  // open: load, D, count, carry, clr
  Comparator #(.mode("unsigned")) comparator_1 (.a(counter_1_q), .b(8'h1), .gt(comparator_1_gt));  // open: eq, lt
  Multiplexer #(.select(5)) multiplexer_1 (
    .in0(in_1[0]), .in1(in_1[1]), .in2(in_1[2]), .in3(in_1[3]), .in4(in_1[4]), .in5(in_1[5]), .in6(in_1[6]),
    .in7(in_1[7]), .in8(in_1[8]), .in9(in_1[9]), .in10(in_1[10]), .in11(in_1[11]), .in12(in_1[12]),
    .in13(in_1[13]), .in14(in_1[14]), .in15(in_1[15]), .in16(in_1[16]), .in17(in_1[17]), .in18(in_1[18]),
    .in19(in_1[19]), .in20(in_1[20]), .in21(in_1[21]), .in22(in_1[22]), .in23(in_1[23]), .in24(in_1[24]),
    .in25(in_1[25]), .in26(in_1[26]), .in27(in_1[27]), .in28(in_1[28]), .in29(in_1[29]), .in30(in_1[30]),
    .in31(in_1[31]), .out(multiplexer_1_out), .sel(counter_2_q));  // open: en
  Comparator #(.mode("unsigned")) comparator_2 (.a(counter_3_q), .b(8'h1), .gt(comparator_2_gt));  // open: eq, lt
  Comparator #(.width(32), .mode("unsigned")) comparator_3 (
    .a(counter_4_q), .b(32'h2f), .eq(comparator_3_eq));  // open: gt, lt
  Register #(.width(1)) register_1 (.D(comparator_3_eq), .Q(register_1_q), .clk(clock_1_out));  // open: en, clr
  Comparator #(.width(1), .mode("unsigned")) comparator_4 (
    .a(multiplexer_1_out), .b(1'b1), .eq(comparator_4_eq));  // open: gt, lt
  Multiplexer #(.width(32)) multiplexer_2 (
    .in0(32'h1), .in1(register_4_q), .out(multiplexer_2_out), .sel(comparator_1_gt));  // open: en
  Multiplexer #(.width(32)) multiplexer_3 (
    .in0({32{1'b0}}), .in1(register_5_q), .out(multiplexer_3_out), .sel(comparator_1_gt));  // open: en
  Multiplexer #(.width(32)) multiplexer_4 (
    .in0({32{1'b0}}), .in1(register_6_q), .out(multiplexer_4_out), .sel(comparator_1_gt));  // open: en
  Multiplexer #(.width(32)) multiplexer_5 (
    .in0(32'h1), .in1(register_7_q), .out(multiplexer_5_out), .sel(comparator_1_gt));  // open: en
  Register #(.width(1)) register_2 (.D(comparator_4_eq), .Q(register_2_q), .clk(clock_1_out));  // open: en, clr
  Multiplexer #(.width(32)) multiplexer_6 (
    .in0(32'h1), .in1(register_8_q), .out(multiplexer_6_out), .sel(comparator_2_gt));  // open: en
  Multiplexer #(.width(32)) multiplexer_7 (
    .in0(32'h1), .in1(register_9_q), .out(multiplexer_7_out), .sel(comparator_2_gt));  // open: en
  Multiplexer #(.width(32)) multiplexer_8 (
    .in0(32'h1), .in1(register_10_q), .out(multiplexer_8_out), .sel(comparator_2_gt));  // open: en
  Multiplexer #(.width(32)) multiplexer_9 (
    .in0({32{1'b0}}), .in1(register_11_q), .out(multiplexer_9_out), .sel(comparator_2_gt));  // open: en
  Register #(.width(32)) register_3 (.D(ans_1_out_12), .en(register_1_q), .Q(out_2), .clk(clock_1_out));  // open: clr
  res res_1 (
    .in_1(multiplexer_6_out), .in_2(multiplexer_7_out), .in_3(multiplexer_8_out), .in_4(multiplexer_9_out),
    .out_5(res_1_out_5), .out_6(res_1_out_6), .out_7(res_1_out_7), .out_8(res_1_out_8));
  Register #(.width(32)) register_4 (.D(ans_1_out_10), .Q(register_4_q), .clk(clock_1_out));  // open: en, clr
  Register #(.width(32)) register_5 (.D(ans_1_out_11), .Q(register_5_q), .clk(clock_1_out));  // open: en, clr
  ans ans_1 (
    .in_1(register_2_q), .in_2(multiplexer_2_out), .in_3(multiplexer_6_out), .in_4(multiplexer_3_out),
    .in_5(multiplexer_7_out), .in_6(multiplexer_4_out), .in_7(multiplexer_8_out), .in_8(multiplexer_5_out),
    .in_9(multiplexer_9_out), .out_10(ans_1_out_10), .out_11(ans_1_out_11), .out_12(ans_1_out_12),
    .out_13(ans_1_out_13));
  Register #(.width(32)) register_6 (.D(ans_1_out_12), .Q(register_6_q), .clk(clock_1_out));  // open: en, clr
  Register #(.width(32)) register_7 (.D(ans_1_out_13), .Q(register_7_q), .clk(clock_1_out));  // open: en, clr
  Register #(.width(32)) register_8 (.D(res_1_out_5), .Q(register_8_q), .clk(clock_1_out));  // open: en, clr
  Register #(.width(32)) register_9 (.D(res_1_out_6), .Q(register_9_q), .clk(clock_1_out));  // open: en, clr
  Register #(.width(32)) register_10 (.D(res_1_out_7), .Q(register_10_q), .clk(clock_1_out));  // open: en, clr
  Register #(.width(32)) register_11 (.D(res_1_out_8), .Q(register_11_q), .clk(clock_1_out));  // open: en, clr

  // Notes on the sheet:
  //   res
  //   ans
endmodule

module ans (
  input  in_1,
  input  [31:0] in_2,
  input  [31:0] in_3,
  input  [31:0] in_4,
  input  [31:0] in_5,
  input  [31:0] in_6,
  input  [31:0] in_7,
  input  [31:0] in_8,
  input  [31:0] in_9,
  output [31:0] out_10,
  output [31:0] out_11,
  output [31:0] out_12,
  output [31:0] out_13
);

  wire [31:0] multiplexer_1_out, multiplexer_2_out, multiplexer_3_out, multiplexer_4_out, multiplier_1_out,
       multiplier_2_out, multiplier_3_out, multiplier_4_out, multiplier_5_out, multiplier_6_out,
       multiplier_7_out, multiplier_8_out;

  Multiplexer #(.width(32)) multiplexer_1 (.in0(32'h1), .in1(in_3), .out(multiplexer_1_out), .sel(in_1));  // open: en
  Multiplexer #(.width(32)) multiplexer_2 (
    .in0({32{1'b0}}), .in1(in_5), .out(multiplexer_2_out), .sel(in_1));  // open: en
  Multiplexer #(.width(32)) multiplexer_3 (
    .in0({32{1'b0}}), .in1(in_7), .out(multiplexer_3_out), .sel(in_1));  // open: en
  Multiplexer #(.width(32)) multiplexer_4 (.in0(32'h1), .in1(in_9), .out(multiplexer_4_out), .sel(in_1));  // open: en
  Multiplier #(.width(32)) multiplier_1 (.a(multiplexer_1_out), .b(in_2), .out(multiplier_1_out));  // open: cin, cout
  Multiplier #(.width(32)) multiplier_2 (.a(multiplexer_3_out), .b(in_4), .out(multiplier_2_out));  // open: cin, cout
  Multiplier #(.width(32)) multiplier_3 (.a(multiplexer_2_out), .b(in_2), .out(multiplier_3_out));  // open: cin, cout
  Multiplier #(.width(32)) multiplier_4 (.a(multiplexer_4_out), .b(in_4), .out(multiplier_4_out));  // open: cin, cout
  Multiplier #(.width(32)) multiplier_5 (.a(multiplexer_1_out), .b(in_6), .out(multiplier_5_out));  // open: cin, cout
  Multiplier #(.width(32)) multiplier_6 (.a(multiplexer_3_out), .b(in_8), .out(multiplier_6_out));  // open: cin, cout
  Multiplier #(.width(32)) multiplier_7 (.a(multiplexer_2_out), .b(in_6), .out(multiplier_7_out));  // open: cin, cout
  Multiplier #(.width(32)) multiplier_8 (.a(multiplexer_4_out), .b(in_8), .out(multiplier_8_out));  // open: cin, cout
  Adder #(.width(32)) adder_1 (.a(multiplier_1_out), .b(multiplier_2_out), .out(out_10));  // open: cin, cout
  Adder #(.width(32)) adder_2 (.a(multiplier_3_out), .b(multiplier_4_out), .out(out_11));  // open: cin, cout
  Adder #(.width(32)) adder_3 (.a(multiplier_5_out), .b(multiplier_6_out), .out(out_12));  // open: cin, cout
  Adder #(.width(32)) adder_4 (.a(multiplier_7_out), .b(multiplier_8_out), .out(out_13));  // open: cin, cout

  // Notes on the sheet:
  //   两个矩阵相乘 即ans=ans*res
  //   左侧输入一列
  //   加上多路选择器
  //   输出为res矩阵
  //   右侧输入一列
  //   为ans矩阵
endmodule

module res (
  input  [31:0] in_1,
  input  [31:0] in_2,
  input  [31:0] in_3,
  input  [31:0] in_4,
  output [31:0] out_5,
  output [31:0] out_6,
  output [31:0] out_7,
  output [31:0] out_8
);

  wire [31:0] multiplier_1_out, multiplier_2_out, multiplier_3_out, multiplier_4_out, multiplier_5_out,
       multiplier_6_out, multiplier_7_out, multiplier_8_out;

  Multiplier #(.width(32)) multiplier_1 (.a(in_1), .b(in_1), .out(multiplier_1_out));  // open: cin, cout
  Multiplier #(.width(32)) multiplier_2 (.a(in_2), .b(in_3), .out(multiplier_2_out));  // open: cin, cout
  Multiplier #(.width(32)) multiplier_3 (.a(in_1), .b(in_2), .out(multiplier_3_out));  // open: cin, cout
  Multiplier #(.width(32)) multiplier_4 (.a(in_2), .b(in_4), .out(multiplier_4_out));  // open: cin, cout
  Multiplier #(.width(32)) multiplier_5 (.a(in_3), .b(in_1), .out(multiplier_5_out));  // open: cin, cout
  Multiplier #(.width(32)) multiplier_6 (.a(in_4), .b(in_3), .out(multiplier_6_out));  // open: cin, cout
  Multiplier #(.width(32)) multiplier_7 (.a(in_3), .b(in_2), .out(multiplier_7_out));  // open: cin, cout
  Multiplier #(.width(32)) multiplier_8 (.a(in_4), .b(in_4), .out(multiplier_8_out));  // open: cin, cout
  Adder #(.width(32)) adder_1 (.a(multiplier_1_out), .b(multiplier_2_out), .out(out_5));  // open: cin, cout
  Adder #(.width(32)) adder_2 (.a(multiplier_3_out), .b(multiplier_4_out), .out(out_6));  // open: cin, cout
  Adder #(.width(32)) adder_3 (.a(multiplier_5_out), .b(multiplier_6_out), .out(out_7));  // open: cin, cout
  Adder #(.width(32)) adder_4 (.a(multiplier_7_out), .b(multiplier_8_out), .out(out_8));  // open: cin, cout

  // Notes on the sheet:
  //   该电路图为矩阵自身的平方 即res=res*res
  //   第一行第一列
  //   第一行第二列
  //   第二行第一列
  //   第二行第二列
endmodule
