// Logisim project P3.circ as structural Verilog
module main (
  input  in_1,
  output [31:0] out_2
);

  wire clk;

  Clock clock_1 (.out(clk));

  // Other names for the same wires on the sheet: Instr[31:0] = out_2; reset = in_1
endmodule

module ALU (
  input  [31:0] A,
  input  [31:0] B,
  input  [3:0] ALU_op,
  output [31:0] Result,
  output Zero
);

  wire bitselector_1_out, comparator_1_eq, comparator_1_lt, comparator_2_lt, comparator_3_gt, not_2_out,
       not_3_out;
  wire [4:0] bit_extender_3_out;
  wire [31:0] _0, _1, _2, _3, _4, _5, _6, _7, _8, _9, _10, _11, _12, _13, _14, _15;

  BitSelector #(.width(32)) bitselector_1 (.in(A), .out(bitselector_1_out), .sel({5{1'b1}}));
  Adder #(.width(32)) adder_1 (.a(A), .b(B), .out(_2));  // open: cin, cout
  Subtractor #(.width(32)) subtractor_1 (.a(A), .b(B), .out(_3));  // open: bin, bout
  assign _4 = A & B;  // AND_Gate and_1, 32 bits wide
  assign _5 = A | B;  // OR_Gate or_1, 32 bits wide
  assign _7 = ~_5;  // NOT_Gate not_1, 32 bits wide
  assign _6 = A ^ B;  // XOR_Gate xor_1, 32 bits wide
  assign _1 = {{31{1'b0}}, bitselector_1_out};  // Bit_Extender bit_extender_1
  not not_2 (not_2_out, bitselector_1_out);
  assign _0 = {{31{1'b0}}, not_2_out};  // Bit_Extender bit_extender_2
  Bit_Extender #(.in_width(32), .out_width(5)) bit_extender_3 (.in(A), .out(bit_extender_3_out));
  Comparator #(.width(32)) comparator_1 (.a(A), .b(B), .eq(comparator_1_eq), .lt(comparator_1_lt));  // open: gt
  Comparator #(.width(32)) comparator_2 (.a(A), .b(B), .lt(comparator_2_lt));  // open: gt, eq
  Comparator #(.width(32)) comparator_3 (.a(A), .b({32{1'b0}}), .gt(comparator_3_gt));  // open: eq, lt
  Shifter #(.width(32), .shift("lr")) shifter_1 (.in(B), .\dist (bit_extender_3_out), .out(_8));
  Shifter #(.width(32), .shift("ar")) shifter_2 (.in(B), .\dist (bit_extender_3_out), .out(_9));
  Shifter #(.width(32)) shifter_3 (.in(B), .\dist (bit_extender_3_out), .out(_10));
  assign _11 = {{31{1'b0}}, comparator_1_eq};  // Bit_Extender bit_extender_4
  assign _12 = {{31{1'b0}}, comparator_1_lt};  // Bit_Extender bit_extender_5
  assign _13 = {{31{1'b0}}, comparator_2_lt};  // Bit_Extender bit_extender_6
  assign _14 = {{31{1'b0}}, comparator_3_gt};  // Bit_Extender bit_extender_7
  not not_3 (not_3_out, comparator_3_gt);
  assign _15 = {{31{1'b0}}, not_3_out};  // Bit_Extender bit_extender_8
  Multiplexer #(.select(4), .width(32)) multiplexer_1 (
    .in0(_0), .in1(_1), .in2(_2), .in3(_3), .in4(_4), .in5(_5), .in6(_6), .in7(_7), .in8(_8), .in9(_9),
    .in10(_10), .in11(_11), .in12(_12), .in13(_13), .in14(_14), .in15(_15), .out(Result), .sel(ALU_op));  // open: en
  Comparator #(.width(32)) comparator_4 (.a(Result), .b({32{1'b0}}), .eq(Zero));  // open: gt, lt
endmodule

module Extender (
  input  [1:0] ExtOp,
  input  [15:0] Imm,
  output [31:0] ImmOut
);

  wire [31:0] bit_extender_1_out, bit_extender_2_out, shifter_1_out;

  assign bit_extender_1_out = {{16{Imm[15]}}, Imm};  // Bit_Extender bit_extender_1
  assign bit_extender_2_out = {{16{1'b0}}, Imm};  // Bit_Extender bit_extender_2
  Shifter #(.width(32)) shifter_1 (.in(bit_extender_1_out), .\dist (5'b00010), .out(shifter_1_out));
  Multiplexer #(.select(2), .width(32)) multiplexer_1 (
    .in0(bit_extender_1_out), .in1(bit_extender_2_out), .in2({Imm, {16{1'b0}}}), .in3(shifter_1_out),
    .out(ImmOut), .sel(ExtOp));  // open: en
endmodule

module Controller (
  input  [5:0] Op,
  input  Nop
);

  wire [10:0] Mid;

  not not_1 (Mid[10], Op[5]);
  not not_2 (Mid[8], Op[4]);
  not not_3 (Mid[6], Op[3]);
  not not_4 (Mid[4], Op[2]);
  not not_5 (Mid[0], Op[0]);
  not not_6 (Mid[2], Op[1]);

  // Other names for the same wires on the sheet: Mid (some bits) = Op
endmodule

module ALUwithOver (
  input  [31:0] A,
  input  [31:0] B,
  input  [3:0] ALU_op,
  output [31:0] Result,
  output Zero,
  output Overflow
);

  wire _01, _02, _03, bitselector_4_out, bitselector_5_out, comparator_1_eq, comparator_1_lt,
       comparator_2_lt, comparator_3_gt, multiplexer_1_out, multiplexer_2_out, multiplexer_3_out, not_2_out,
       not_3_out, xor_2_out, xor_3_out, xor_4_out;
  wire [4:0] bit_extender_3_out;
  wire [31:0] _0, _1, _2, _3, _4, _5, _6, _7, _8, _9, _10, _11, _12, _13, _14, _15;

  BitSelector #(.width(32)) bitselector_1 (.in(A), .out(_01), .sel({5{1'b1}}));
  Adder #(.width(32)) adder_1 (.a(A), .b(B), .out(_2));  // open: cin, cout
  BitSelector #(.width(32)) bitselector_2 (.in(_2), .out(_02), .sel({5{1'b1}}));
  Subtractor #(.width(32)) subtractor_1 (.a(A), .b(B), .out(_3));  // open: bin, bout
  BitSelector #(.width(32)) bitselector_3 (.in(_3), .out(_03), .sel({5{1'b1}}));
  assign _4 = A & B;  // AND_Gate and_1, 32 bits wide
  assign _5 = A | B;  // OR_Gate or_1, 32 bits wide
  assign _7 = ~_5;  // NOT_Gate not_1, 32 bits wide
  assign _6 = A ^ B;  // XOR_Gate xor_1, 32 bits wide
  assign _1 = {{31{1'b0}}, _01};  // Bit_Extender bit_extender_1
  assign _0 = {{31{1'b0}}, not_2_out};  // Bit_Extender bit_extender_2
  not not_2 (not_2_out, _01);
  Bit_Extender #(.in_width(32), .out_width(5)) bit_extender_3 (.in(A), .out(bit_extender_3_out));
  Comparator #(.width(32)) comparator_1 (.a(A), .b(B), .eq(comparator_1_eq), .lt(comparator_1_lt));  // open: gt
  Comparator #(.width(32)) comparator_2 (.a(A), .b(B), .lt(comparator_2_lt));  // open: gt, eq
  Comparator #(.width(32)) comparator_3 (.a(A), .b({32{1'b0}}), .gt(comparator_3_gt));  // open: eq, lt
  Shifter #(.width(32), .shift("lr")) shifter_1 (.in(B), .\dist (bit_extender_3_out), .out(_8));
  Shifter #(.width(32), .shift("ar")) shifter_2 (.in(B), .\dist (bit_extender_3_out), .out(_9));
  Shifter #(.width(32)) shifter_3 (.in(B), .\dist (bit_extender_3_out), .out(_10));
  BitSelector #(.width(32)) bitselector_4 (.in(A), .out(bitselector_4_out), .sel({5{1'b1}}));
  BitSelector #(.width(32)) bitselector_5 (.in(B), .out(bitselector_5_out), .sel({5{1'b1}}));
  xor xor_2 (xor_2_out, bitselector_4_out, bitselector_5_out);
  assign _11 = {{31{1'b0}}, comparator_1_eq};  // Bit_Extender bit_extender_4
  assign _12 = {{31{1'b0}}, comparator_1_lt};  // Bit_Extender bit_extender_5
  assign _13 = {{31{1'b0}}, comparator_2_lt};  // Bit_Extender bit_extender_6
  assign _14 = {{31{1'b0}}, comparator_3_gt};  // Bit_Extender bit_extender_7
  assign _15 = {{31{1'b0}}, not_3_out};  // Bit_Extender bit_extender_8
  not not_3 (not_3_out, comparator_3_gt);
  xor xor_3 (xor_3_out, _01, _02);
  xor xor_4 (xor_4_out, _01, _03);
  Multiplexer multiplexer_1 (.in0(xor_3_out), .in1(1'b0), .out(multiplexer_1_out), .sel(xor_2_out));  // open: en
  Multiplexer multiplexer_2 (.in0(1'b0), .in1(xor_4_out), .out(multiplexer_2_out), .sel(xor_2_out));  // open: en
  Multiplexer #(.select(2)) multiplexer_3 (
    .in0(1'b0), .in1(1'b0), .in2(multiplexer_1_out), .in3(multiplexer_2_out), .out(multiplexer_3_out),
    .sel(ALU_op[1:0]));  // open: en
  Multiplexer #(.select(4), .width(32)) multiplexer_4 (
    .in0(_0), .in1(_1), .in2(_2), .in3(_3), .in4(_4), .in5(_5), .in6(_6), .in7(_7), .in8(_8), .in9(_9),
    .in10(_10), .in11(_11), .in12(_12), .in13(_13), .in14(_14), .in15(_15), .out(Result), .sel(ALU_op));  // open: en
  Multiplexer #(.select(2)) multiplexer_5 (
    .in0(multiplexer_3_out), .in1(1'b0), .in2(1'b0), .in3(1'b0), .out(Overflow), .sel(ALU_op[3:2]));  // open: en
  Comparator #(.width(32)) comparator_4 (.a(Result), .b({32{1'b0}}), .eq(Zero));  // open: gt, lt
endmodule
